// Logisim project microfpgamux.circ as structural Verilog: 2 circuits, main circuit muxcore
module muxcore (
);

  wire [63:0] muxreg_1_o0, muxreg_1_o1, muxreg_1_o2, muxreg_1_o3, muxreg_1_o4, muxreg_1_o5, muxreg_1_o6,
       muxreg_1_o7, muxreg_1_o8, muxreg_1_o9, muxreg_1_o10, muxreg_1_o11, muxreg_1_o12, muxreg_1_o13,
       muxreg_1_o14, muxreg_1_o15, muxreg_2_o0, muxreg_2_o1, muxreg_2_o2, muxreg_2_o3, muxreg_2_o4,
       muxreg_2_o5, muxreg_2_o6, muxreg_2_o7, muxreg_2_o8, muxreg_2_o9, muxreg_2_o10, muxreg_2_o11,
       muxreg_2_o12, muxreg_2_o13, muxreg_2_o14, muxreg_2_o15, muxreg_3_o0, muxreg_3_o1, muxreg_3_o2,
       muxreg_3_o3, muxreg_3_o4, muxreg_3_o5, muxreg_3_o6, muxreg_3_o7, muxreg_3_o8, muxreg_3_o9,
       muxreg_3_o10, muxreg_3_o11, muxreg_3_o12, muxreg_3_o13, muxreg_3_o14, muxreg_3_o15;

  // Probe on muxreg_1_o0
  muxreg muxreg_1 (
    .A0({6{1'b0}}), .A1(6'b000001), .A2(6'b000010), .A3(6'b000011), .A4(6'b000100), .A5(6'b000101),
    .A6(6'b000110), .A7(6'b000111), .A8(6'b111000), .A9(6'b111001), .A10(6'b111010), .A11(6'b111011),
    .A12(6'b111100), .A13(6'b111101), .A14(6'b111110), .A15({6{1'b1}}), .D0({64{1'b0}}), .D1(64'h1111),
    .D2(64'h2222), .D3(64'h3333), .D4(64'h4444), .D5(64'h5555), .D6(64'h6666), .D7(64'h7777), .D8(64'h8888),
    .D9(64'h9999), .D10(64'haaaa), .D11(64'hbbbb), .D12(64'hcccc), .D13(64'hdddd), .D14(64'heeee),
    .D15(64'hffff), .LE0(1'b1), .LE1(1'b1), .LE2(1'b1), .LE3(1'b1), .LE4(1'b1), .LE5(1'b1), .LE6(1'b1),
    .LE7(1'b1), .LE8(1'b1), .LE9(1'b1), .LE10(1'b1), .LE11(1'b1), .LE12(1'b1), .LE13(1'b1), .LE14(1'b1),
    .LE15(1'b1), .O0(muxreg_1_o0), .O1(muxreg_1_o1), .O2(muxreg_1_o2), .O3(muxreg_1_o3), .O4(muxreg_1_o4),
    .O5(muxreg_1_o5), .O6(muxreg_1_o6), .O7(muxreg_1_o7), .O8(muxreg_1_o8), .O9(muxreg_1_o9),
    .O10(muxreg_1_o10), .O11(muxreg_1_o11), .O12(muxreg_1_o12), .O13(muxreg_1_o13), .O14(muxreg_1_o14),
    .O15(muxreg_1_o15));
  // Probe on muxreg_1_o1
  // Probe on muxreg_1_o2
  // Probe on muxreg_1_o3
  // Probe on muxreg_1_o4
  // Probe on muxreg_1_o5
  // Probe on muxreg_1_o6
  // Probe on muxreg_1_o7
  // Probe on muxreg_1_o8
  // Probe on muxreg_1_o9
  // Probe on muxreg_1_o10
  // Probe on muxreg_1_o11
  // Probe on muxreg_1_o12
  // Probe on muxreg_1_o13
  // Probe on muxreg_1_o14
  // Probe on muxreg_1_o15
  // Probe on muxreg_2_o0
  muxreg muxreg_2 (
    .A0({6{1'b0}}), .A1({6{1'b0}}), .A2(6'b111011), .A3(6'b000011), .A4(6'b000100), .A5(6'b111100),
    .A6({6{1'b0}}), .A7(6'b000111), .A8(6'b000011), .A9({6{1'b1}}), .A10(6'b111010), .A11({6{1'b0}}),
    .A12(6'b111100), .A13(6'b111101), .A14(6'b000011), .A15(6'b000010), .D0({64{1'b0}}), .D1(64'h1111),
    .D2(64'h2222), .D3(64'h3333), .D4(64'h4444), .D5(64'h5555), .D6(64'h6666), .D7(64'h7777), .D8(64'h8888),
    .D9(64'h9999), .D10(64'haaaa), .D11(64'hbbbb), .D12(64'hcccc), .D13(64'hdddd), .D14(64'heeee),
    .D15(64'hffff), .LE0(1'b1), .LE1(1'b1), .LE2(1'b1), .LE3(1'b1), .LE4(1'b1), .LE5(1'b1), .LE6(1'b1),
    .LE7(1'b1), .LE8(1'b1), .LE9(1'b1), .LE10(1'b1), .LE11(1'b1), .LE12(1'b1), .LE13(1'b1), .LE14(1'b1),
    .LE15(1'b1), .O0(muxreg_2_o0), .O1(muxreg_2_o1), .O2(muxreg_2_o2), .O3(muxreg_2_o3), .O4(muxreg_2_o4),
    .O5(muxreg_2_o5), .O6(muxreg_2_o6), .O7(muxreg_2_o7), .O8(muxreg_2_o8), .O9(muxreg_2_o9),
    .O10(muxreg_2_o10), .O11(muxreg_2_o11), .O12(muxreg_2_o12), .O13(muxreg_2_o13), .O14(muxreg_2_o14),
    .O15(muxreg_2_o15));
  // Probe on muxreg_2_o1
  // Probe on muxreg_2_o2
  // Probe on muxreg_2_o3
  // Probe on muxreg_2_o4
  // Probe on muxreg_2_o5
  // Probe on muxreg_2_o6
  // Probe on muxreg_2_o7
  // Probe on muxreg_2_o8
  // Probe on muxreg_2_o9
  // Probe on muxreg_2_o10
  // Probe on muxreg_2_o11
  // Probe on muxreg_2_o12
  // Probe on muxreg_2_o13
  // Probe on muxreg_2_o14
  // Probe on muxreg_2_o15
  // Probe on muxreg_3_o0
  muxreg muxreg_3 (
    .A0({6{1'b0}}), .A1({6{1'b0}}), .A2(6'b111011), .A3(6'b000011), .A4(6'b000100), .A5(6'b111100),
    .A6({6{1'b0}}), .A7(6'b000111), .A8(6'b000011), .A9({6{1'b1}}), .A10(6'b111010), .A11({6{1'b0}}),
    .A12(6'b111100), .A13(6'b111101), .A14(6'b000011), .A15(6'b000010), .D0({64{1'b0}}), .D1(64'h1111),
    .D2(64'h2222), .D3(64'h3333), .D4(64'h4444), .D5(64'h5555), .D6(64'h6666), .D7(64'h7777), .D8(64'h8888),
    .D9(64'h9999), .D10(64'haaaa), .D11(64'hbbbb), .D12(64'hcccc), .D13(64'hdddd), .D14(64'heeee),
    .D15(64'hffff), .LE0(1'b0), .LE1(1'b1), .LE2(1'b1), .LE3(1'b1), .LE4(1'b0), .LE5(1'b1), .LE6(1'b1),
    .LE7(1'b1), .LE8(1'b0), .LE9(1'b0), .LE10(1'b1), .LE11(1'b1), .LE12(1'b0), .LE13(1'b1), .LE14(1'b0),
    .LE15(1'b1), .O0(muxreg_3_o0), .O1(muxreg_3_o1), .O2(muxreg_3_o2), .O3(muxreg_3_o3), .O4(muxreg_3_o4),
    .O5(muxreg_3_o5), .O6(muxreg_3_o6), .O7(muxreg_3_o7), .O8(muxreg_3_o8), .O9(muxreg_3_o9),
    .O10(muxreg_3_o10), .O11(muxreg_3_o11), .O12(muxreg_3_o12), .O13(muxreg_3_o13), .O14(muxreg_3_o14),
    .O15(muxreg_3_o15));
  // Probe on muxreg_3_o1
  // Probe on muxreg_3_o2
  // Probe on muxreg_3_o3
  // Probe on muxreg_3_o4
  // Probe on muxreg_3_o5
  // Probe on muxreg_3_o6
  // Probe on muxreg_3_o7
  // Probe on muxreg_3_o8
  // Probe on muxreg_3_o9
  // Probe on muxreg_3_o10
  // Probe on muxreg_3_o11
  // Probe on muxreg_3_o12
  // Probe on muxreg_3_o13
  // Probe on muxreg_3_o14
  // Probe on muxreg_3_o15
endmodule

module muxreg (
  input  [5:0] A0,
  input  [5:0] A1,
  input  [5:0] A2,
  input  [5:0] A3,
  input  [5:0] A4,
  input  [5:0] A5,
  input  [5:0] A6,
  input  [5:0] A7,
  input  [5:0] A8,
  input  [5:0] A9,
  input  [5:0] A10,
  input  [5:0] A11,
  input  [5:0] A12,
  input  [5:0] A13,
  input  [5:0] A14,
  input  [5:0] A15,
  input  [63:0] D0,
  input  [63:0] D1,
  input  [63:0] D2,
  input  [63:0] D3,
  input  [63:0] D4,
  input  [63:0] D5,
  input  [63:0] D6,
  input  [63:0] D7,
  input  [63:0] D8,
  input  [63:0] D9,
  input  [63:0] D10,
  input  [63:0] D11,
  input  [63:0] D12,
  input  [63:0] D13,
  input  [63:0] D14,
  input  [63:0] D15,
  input  LE0,
  input  LE1,
  input  LE2,
  input  LE3,
  input  LE4,
  input  LE5,
  input  LE6,
  input  LE7,
  input  LE8,
  input  LE9,
  input  LE10,
  input  LE11,
  input  LE12,
  input  LE13,
  input  LE14,
  input  LE15,
  output [63:0] O0,
  output [63:0] O1,
  output [63:0] O2,
  output [63:0] O3,
  output [63:0] O4,
  output [63:0] O5,
  output [63:0] O6,
  output [63:0] O7,
  output [63:0] O8,
  output [63:0] O9,
  output [63:0] O10,
  output [63:0] O11,
  output [63:0] O12,
  output [63:0] O13,
  output [63:0] O14,
  output [63:0] O15
);

  wire A0L0, A0L1, A0L2, A0L3, A0L4, A0L5, A0L6, A0L7, A0L8, A0L9, A0L10, A0L11, A0L12, A0L13, A0L14, A0L15,
       A0L16, A0L17, A0L18, A0L19, A0L20, A0L21, A0L22, A0L23, A0L24, A0L25, A0L26, A0L27, A0L28, A0L29,
       A0L30, A0L31, A0L32, A0L33, A0L34, A0L35, A0L36, A0L37, A0L38, A0L39, A0L40, A0L41, A0L42, A0L43,
       A0L44, A0L45, A0L46, A0L47, A0L48, A0L49, A0L50, A0L51, A0L52, A0L53, A0L54, A0L55, A0L56, A0L57,
       A0L58, A0L59, A0L60, A0L61, A0L62, A0L63, A1L0, A1L1, A1L2, A1L3, A1L4, A1L5, A1L6, A1L7, A1L8, A1L9,
       A1L10, A1L11, A1L12, A1L13, A1L14, A1L15, A1L16, A1L17, A1L18, A1L19, A1L20, A1L21, A1L22, A1L23,
       A1L24, A1L25, A1L26, A1L27, A1L28, A1L29, A1L30, A1L31, A1L32, A1L33, A1L34, A1L35, A1L36, A1L37,
       A1L38, A1L39, A1L40, A1L41, A1L42, A1L43, A1L44, A1L45, A1L46, A1L47, A1L48, A1L49, A1L50, A1L51,
       A1L52, A1L53, A1L54, A1L55, A1L56, A1L57, A1L58, A1L59, A1L60, A1L61, A1L62, A1L63, clock_1_out,
       clock_2_out, clock_3_out, clock_4_out, clock_5_out, clock_6_out, clock_7_out, clock_8_out,
       clock_9_out, clock_10_out, clock_11_out, clock_12_out, clock_13_out, clock_14_out, clock_15_out,
       clock_16_out, clock_17_out, clock_18_out, clock_19_out, clock_20_out, clock_21_out, clock_22_out,
       clock_23_out, clock_24_out, clock_25_out, clock_26_out, clock_27_out, clock_28_out, clock_29_out,
       clock_30_out, clock_31_out, clock_32_out, clock_33_out, clock_34_out, clock_35_out, clock_36_out,
       clock_37_out, clock_38_out, clock_39_out, clock_40_out, clock_41_out, clock_42_out, clock_43_out,
       clock_44_out, clock_45_out, clock_46_out, clock_47_out, clock_48_out, clock_49_out, clock_50_out,
       clock_51_out, clock_52_out, clock_53_out, clock_54_out, clock_55_out, clock_56_out, clock_57_out,
       clock_58_out, clock_59_out, clock_60_out, clock_61_out, clock_62_out, clock_63_out, clock_64_out,
       or_2_out, or_4_out, or_6_out, or_8_out, or_10_out, or_12_out, or_14_out, or_16_out, or_18_out,
       or_20_out, or_22_out, or_24_out, or_26_out, or_28_out, or_30_out, or_32_out, or_34_out, or_36_out,
       or_38_out, or_40_out, or_42_out, or_44_out, or_46_out, or_48_out, or_50_out, or_52_out, or_54_out,
       or_56_out, or_58_out, or_60_out, or_62_out, or_64_out, or_66_out, or_68_out, or_70_out, or_72_out,
       or_74_out, or_76_out, or_78_out, or_80_out, or_82_out, or_84_out, or_86_out, or_88_out, or_90_out,
       or_92_out, or_94_out, or_96_out, or_98_out, or_100_out, or_102_out, or_104_out, or_106_out,
       or_108_out, or_110_out, or_112_out, or_114_out, or_116_out, or_118_out, or_120_out, or_122_out,
       or_124_out, or_126_out, or_128_out;
  wire [63:0] A0R0, A0R1, A0R2, A0R3, A0R4, A0R5, A0R6, A0R7, A0R8, A0R9, A0R10, A0R11, A0R12, A0R13, A0R14,
       A0R15, A0R16, A0R17, A0R18, A0R19, A0R20, A0R21, A0R22, A0R23, A0R24, A0R25, A0R26, A0R27, A0R28,
       A0R29, A0R30, A0R31, A0R32, A0R33, A0R34, A0R35, A0R36, A0R37, A0R38, A0R39, A0R40, A0R41, A0R42,
       A0R43, A0R44, A0R45, A0R46, A0R47, A0R48, A0R49, A0R50, A0R51, A0R52, A0R53, A0R54, A0R55, A0R56,
       A0R57, A0R58, A0R59, A0R60, A0R61, A0R62, A0R63, A1R0, A1R1, A1R2, A1R3, A1R4, A1R5, A1R6, A1R7, A1R8,
       A1R9, A1R10, A1R11, A1R12, A1R13, A1R14, A1R15, A1R16, A1R17, A1R18, A1R19, A1R20, A1R21, A1R22,
       A1R23, A1R24, A1R25, A1R26, A1R27, A1R28, A1R29, A1R30, A1R31, A1R32, A1R33, A1R34, A1R35, A1R36,
       A1R37, A1R38, A1R39, A1R40, A1R41, A1R42, A1R43, A1R44, A1R45, A1R46, A1R47, A1R48, A1R49, A1R50,
       A1R51, A1R52, A1R53, A1R54, A1R55, A1R56, A1R57, A1R58, A1R59, A1R60, A1R61, A1R62, A1R63, or_1_out,
       or_3_out, or_5_out, or_7_out, or_9_out, or_11_out, or_13_out, or_15_out, or_17_out, or_19_out,
       or_21_out, or_23_out, or_25_out, or_27_out, or_29_out, or_31_out, or_33_out, or_35_out, or_37_out,
       or_39_out, or_41_out, or_43_out, or_45_out, or_47_out, or_49_out, or_51_out, or_53_out, or_55_out,
       or_57_out, or_59_out, or_61_out, or_63_out, or_65_out, or_67_out, or_69_out, or_71_out, or_73_out,
       or_75_out, or_77_out, or_79_out, or_81_out, or_83_out, or_85_out, or_87_out, or_89_out, or_91_out,
       or_93_out, or_95_out, or_97_out, or_99_out, or_101_out, or_103_out, or_105_out, or_107_out,
       or_109_out, or_111_out, or_113_out, or_115_out, or_117_out, or_119_out, or_121_out, or_123_out,
       or_125_out, or_127_out, R0, R1, R2, R3, R4, R5, R6, R7, R8, R9, R10, R11, R12, R13, R14, R15, R16,
       R17, R18, R19, R20, R21, R22, R23, R24, R25, R26, R27, R28, R29, R30, R31, R32, R33, R34, R35, R36,
       R37, R38, R39, R40, R41, R42, R43, R44, R45, R46, R47, R48, R49, R50, R51, R52, R53, R54, R55, R56,
       R57, R58, R59, R60, R61, R62, R63;

  Demultiplexer #(.select(6), .width(64)) demultiplexer_1 (
    .out0(A0R0), .out1(A0R1), .out2(A0R2), .out3(A0R3), .out4(A0R4), .out5(A0R5), .out6(A0R6), .out7(A0R7),
    .out8(A0R8), .out9(A0R9), .out10(A0R10), .out11(A0R11), .out12(A0R12), .out13(A0R13), .out14(A0R14),
    .out15(A0R15), .out16(A0R16), .out17(A0R17), .out18(A0R18), .out19(A0R19), .out20(A0R20), .out21(A0R21),
    .out22(A0R22), .out23(A0R23), .out24(A0R24), .out25(A0R25), .out26(A0R26), .out27(A0R27), .out28(A0R28),
    .out29(A0R29), .out30(A0R30), .out31(A0R31), .out32(A0R32), .out33(A0R33), .out34(A0R34), .out35(A0R35),
    .out36(A0R36), .out37(A0R37), .out38(A0R38), .out39(A0R39), .out40(A0R40), .out41(A0R41), .out42(A0R42),
    .out43(A0R43), .out44(A0R44), .out45(A0R45), .out46(A0R46), .out47(A0R47), .out48(A0R48), .out49(A0R49),
    .out50(A0R50), .out51(A0R51), .out52(A0R52), .out53(A0R53), .out54(A0R54), .out55(A0R55), .out56(A0R56),
    .out57(A0R57), .out58(A0R58), .out59(A0R59), .out60(A0R60), .out61(A0R61), .out62(A0R62), .out63(A0R63),
    .in(D0), .sel(A0));
  assign or_1_out = A0R0 | A1R0;  // OR_Gate or_1, 64 bits wide
  Register #(.width(64)) reg0 (.D(or_1_out), .en(or_2_out), .Q(R0), .clk(clock_1_out));  // open: clr
  or or_2 (or_2_out, A0L0, A1L0);
  Clock clock_1 (.out(clock_1_out));
  assign or_3_out = A0R16 | A1R16;  // OR_Gate or_3, 64 bits wide
  Register #(.width(64)) reg16 (.D(or_3_out), .en(or_4_out), .Q(R16), .clk(clock_2_out));  // open: clr
  or or_4 (or_4_out, A0L16, A1L16);
  Clock clock_2 (.out(clock_2_out));
  assign or_5_out = A0R32 | A1R32;  // OR_Gate or_5, 64 bits wide
  Register #(.width(64)) reg32 (.D(or_5_out), .en(or_6_out), .Q(R32), .clk(clock_3_out));  // open: clr
  or or_6 (or_6_out, A0L32, A1L32);
  Clock clock_3 (.out(clock_3_out));
  assign or_7_out = A0R48 | A1R48;  // OR_Gate or_7, 64 bits wide
  Register #(.width(64)) reg48 (.D(or_7_out), .en(or_8_out), .Q(R48), .clk(clock_4_out));  // open: clr
  or or_8 (or_8_out, A0L48, A1L48);
  Clock clock_4 (.out(clock_4_out));
  Demultiplexer #(.select(6)) demultiplexer_2 (
    .out0(A0L0), .out1(A0L1), .out2(A0L2), .out3(A0L3), .out4(A0L4), .out5(A0L5), .out6(A0L6), .out7(A0L7),
    .out8(A0L8), .out9(A0L9), .out10(A0L10), .out11(A0L11), .out12(A0L12), .out13(A0L13), .out14(A0L14),
    .out15(A0L15), .out16(A0L16), .out17(A0L17), .out18(A0L18), .out19(A0L19), .out20(A0L20), .out21(A0L21),
    .out22(A0L22), .out23(A0L23), .out24(A0L24), .out25(A0L25), .out26(A0L26), .out27(A0L27), .out28(A0L28),
    .out29(A0L29), .out30(A0L30), .out31(A0L31), .out32(A0L32), .out33(A0L33), .out34(A0L34), .out35(A0L35),
    .out36(A0L36), .out37(A0L37), .out38(A0L38), .out39(A0L39), .out40(A0L40), .out41(A0L41), .out42(A0L42),
    .out43(A0L43), .out44(A0L44), .out45(A0L45), .out46(A0L46), .out47(A0L47), .out48(A0L48), .out49(A0L49),
    .out50(A0L50), .out51(A0L51), .out52(A0L52), .out53(A0L53), .out54(A0L54), .out55(A0L55), .out56(A0L56),
    .out57(A0L57), .out58(A0L58), .out59(A0L59), .out60(A0L60), .out61(A0L61), .out62(A0L62), .out63(A0L63),
    .in(LE0), .sel(A0));
  assign or_9_out = A0R1 | A1R1;  // OR_Gate or_9, 64 bits wide
  or or_10 (or_10_out, A0L1, A1L1);
  Clock clock_5 (.out(clock_5_out));
  assign or_11_out = A0R17 | A1R17;  // OR_Gate or_11, 64 bits wide
  or or_12 (or_12_out, A0L17, A1L17);
  Clock clock_6 (.out(clock_6_out));
  assign or_13_out = A0R33 | A1R33;  // OR_Gate or_13, 64 bits wide
  or or_14 (or_14_out, A0L33, A1L33);
  Clock clock_7 (.out(clock_7_out));
  assign or_15_out = A0R49 | A1R49;  // OR_Gate or_15, 64 bits wide
  or or_16 (or_16_out, A0L49, A1L49);
  Clock clock_8 (.out(clock_8_out));
  Register #(.width(64)) reg1 (.D(or_9_out), .en(or_10_out), .Q(R1), .clk(clock_5_out));  // open: clr
  Register #(.width(64)) reg17 (.D(or_11_out), .en(or_12_out), .Q(R17), .clk(clock_6_out));  // open: clr
  Register #(.width(64)) reg33 (.D(or_13_out), .en(or_14_out), .Q(R33), .clk(clock_7_out));  // open: clr
  Register #(.width(64)) reg49 (.D(or_15_out), .en(or_16_out), .Q(R49), .clk(clock_8_out));  // open: clr
  assign or_17_out = A0R2 | A1R2;  // OR_Gate or_17, 64 bits wide
  Register #(.width(64)) reg2 (.D(or_17_out), .en(or_18_out), .Q(R2), .clk(clock_9_out));  // open: clr
  or or_18 (or_18_out, A0L2, A1L2);
  Clock clock_9 (.out(clock_9_out));
  assign or_19_out = A0R18 | A1R18;  // OR_Gate or_19, 64 bits wide
  Register #(.width(64)) reg18 (.D(or_19_out), .en(or_20_out), .Q(R18), .clk(clock_10_out));  // open: clr
  or or_20 (or_20_out, A0L18, A1L18);
  Clock clock_10 (.out(clock_10_out));
  assign or_21_out = A0R34 | A1R34;  // OR_Gate or_21, 64 bits wide
  Register #(.width(64)) reg34 (.D(or_21_out), .en(or_22_out), .Q(R34), .clk(clock_11_out));  // open: clr
  or or_22 (or_22_out, A0L34, A1L34);
  Clock clock_11 (.out(clock_11_out));
  assign or_23_out = A0R50 | A1R50;  // OR_Gate or_23, 64 bits wide
  Register #(.width(64)) reg50 (.D(or_23_out), .en(or_24_out), .Q(R50), .clk(clock_12_out));  // open: clr
  or or_24 (or_24_out, A0L50, A1L50);
  Clock clock_12 (.out(clock_12_out));
  Multiplexer #(.select(6), .width(64)) multiplexer_1 (
    .in0(R0), .in1(R1), .in2(R2), .in3(R3), .in4(R4), .in5(R5), .in6(R6), .in7(R7), .in8(R8), .in9(R9),
    .in10(R10), .in11(R11), .in12(R12), .in13(R13), .in14(R14), .in15(R15), .in16(R16), .in17(R17),
    .in18(R18), .in19(R19), .in20(R20), .in21(R21), .in22(R22), .in23(R23), .in24(R24), .in25(R25),
    .in26(R26), .in27(R27), .in28(R28), .in29(R29), .in30(R30), .in31(R31), .in32(R32), .in33(R33),
    .in34(R34), .in35(R35), .in36(R36), .in37(R37), .in38(R38), .in39(R39), .in40(R40), .in41(R41),
    .in42(R42), .in43(R43), .in44(R44), .in45(R45), .in46(R46), .in47(R47), .in48(R48), .in49(R49),
    .in50(R50), .in51(R51), .in52(R52), .in53(R53), .in54(R54), .in55(R55), .in56(R56), .in57(R57),
    .in58(R58), .in59(R59), .in60(R60), .in61(R61), .in62(R62), .in63(R63), .out(O0), .sel(A0));
  assign or_25_out = A0R3 | A1R3;  // OR_Gate or_25, 64 bits wide
  or or_26 (or_26_out, A0L3, A1L3);
  Clock clock_13 (.out(clock_13_out));
  assign or_27_out = A0R19 | A1R19;  // OR_Gate or_27, 64 bits wide
  or or_28 (or_28_out, A0L19, A1L19);
  Clock clock_14 (.out(clock_14_out));
  assign or_29_out = A0R35 | A1R35;  // OR_Gate or_29, 64 bits wide
  or or_30 (or_30_out, A0L35, A1L35);
  Clock clock_15 (.out(clock_15_out));
  assign or_31_out = A0R51 | A1R51;  // OR_Gate or_31, 64 bits wide
  or or_32 (or_32_out, A0L51, A1L51);
  Clock clock_16 (.out(clock_16_out));
  Register #(.width(64)) reg3 (.D(or_25_out), .en(or_26_out), .Q(R3), .clk(clock_13_out));  // open: clr
  Register #(.width(64)) reg19 (.D(or_27_out), .en(or_28_out), .Q(R19), .clk(clock_14_out));  // open: clr
  Register #(.width(64)) reg35 (.D(or_29_out), .en(or_30_out), .Q(R35), .clk(clock_15_out));  // open: clr
  Register #(.width(64)) reg51 (.D(or_31_out), .en(or_32_out), .Q(R51), .clk(clock_16_out));  // open: clr
  Demultiplexer #(.select(6), .width(64)) demultiplexer_3 (
    .out0(A1R0), .out1(A1R1), .out2(A1R2), .out3(A1R3), .out4(A1R4), .out5(A1R5), .out6(A1R6), .out7(A1R7),
    .out8(A1R8), .out9(A1R9), .out10(A1R10), .out11(A1R11), .out12(A1R12), .out13(A1R13), .out14(A1R14),
    .out15(A1R15), .out16(A1R16), .out17(A1R17), .out18(A1R18), .out19(A1R19), .out20(A1R20), .out21(A1R21),
    .out22(A1R22), .out23(A1R23), .out24(A1R24), .out25(A1R25), .out26(A1R26), .out27(A1R27), .out28(A1R28),
    .out29(A1R29), .out30(A1R30), .out31(A1R31), .out32(A1R32), .out33(A1R33), .out34(A1R34), .out35(A1R35),
    .out36(A1R36), .out37(A1R37), .out38(A1R38), .out39(A1R39), .out40(A1R40), .out41(A1R41), .out42(A1R42),
    .out43(A1R43), .out44(A1R44), .out45(A1R45), .out46(A1R46), .out47(A1R47), .out48(A1R48), .out49(A1R49),
    .out50(A1R50), .out51(A1R51), .out52(A1R52), .out53(A1R53), .out54(A1R54), .out55(A1R55), .out56(A1R56),
    .out57(A1R57), .out58(A1R58), .out59(A1R59), .out60(A1R60), .out61(A1R61), .out62(A1R62), .out63(A1R63),
    .in(D1), .sel(A1));
  assign or_33_out = A0R4 | A1R4;  // OR_Gate or_33, 64 bits wide
  or or_34 (or_34_out, A0L4, A1L4);
  assign or_35_out = A0R20 | A1R20;  // OR_Gate or_35, 64 bits wide
  or or_36 (or_36_out, A0L20, A1L20);
  assign or_37_out = A0R36 | A1R36;  // OR_Gate or_37, 64 bits wide
  or or_38 (or_38_out, A0L36, A1L36);
  assign or_39_out = A0R52 | A1R52;  // OR_Gate or_39, 64 bits wide
  or or_40 (or_40_out, A0L52, A1L52);
  Register #(.width(64)) reg4 (.D(or_33_out), .en(or_34_out), .Q(R4), .clk(clock_17_out));  // open: clr
  Clock clock_17 (.out(clock_17_out));
  Register #(.width(64)) reg20 (.D(or_35_out), .en(or_36_out), .Q(R20), .clk(clock_18_out));  // open: clr
  Clock clock_18 (.out(clock_18_out));
  Register #(.width(64)) reg36 (.D(or_37_out), .en(or_38_out), .Q(R36), .clk(clock_19_out));  // open: clr
  Clock clock_19 (.out(clock_19_out));
  Register #(.width(64)) reg52 (.D(or_39_out), .en(or_40_out), .Q(R52), .clk(clock_20_out));  // open: clr
  Clock clock_20 (.out(clock_20_out));
  assign or_41_out = A0R5 | A1R5;  // OR_Gate or_41, 64 bits wide
  or or_42 (or_42_out, A0L5, A1L5);
  assign or_43_out = A0R21 | A1R21;  // OR_Gate or_43, 64 bits wide
  or or_44 (or_44_out, A0L21, A1L21);
  assign or_45_out = A0R37 | A1R37;  // OR_Gate or_45, 64 bits wide
  or or_46 (or_46_out, A0L37, A1L37);
  assign or_47_out = A0R53 | A1R53;  // OR_Gate or_47, 64 bits wide
  or or_48 (or_48_out, A0L53, A1L53);
  Demultiplexer #(.select(6)) demultiplexer_4 (
    .out0(A1L0), .out1(A1L1), .out2(A1L2), .out3(A1L3), .out4(A1L4), .out5(A1L5), .out6(A1L6), .out7(A1L7),
    .out8(A1L8), .out9(A1L9), .out10(A1L10), .out11(A1L11), .out12(A1L12), .out13(A1L13), .out14(A1L14),
    .out15(A1L15), .out16(A1L16), .out17(A1L17), .out18(A1L18), .out19(A1L19), .out20(A1L20), .out21(A1L21),
    .out22(A1L22), .out23(A1L23), .out24(A1L24), .out25(A1L25), .out26(A1L26), .out27(A1L27), .out28(A1L28),
    .out29(A1L29), .out30(A1L30), .out31(A1L31), .out32(A1L32), .out33(A1L33), .out34(A1L34), .out35(A1L35),
    .out36(A1L36), .out37(A1L37), .out38(A1L38), .out39(A1L39), .out40(A1L40), .out41(A1L41), .out42(A1L42),
    .out43(A1L43), .out44(A1L44), .out45(A1L45), .out46(A1L46), .out47(A1L47), .out48(A1L48), .out49(A1L49),
    .out50(A1L50), .out51(A1L51), .out52(A1L52), .out53(A1L53), .out54(A1L54), .out55(A1L55), .out56(A1L56),
    .out57(A1L57), .out58(A1L58), .out59(A1L59), .out60(A1L60), .out61(A1L61), .out62(A1L62), .out63(A1L63),
    .in(LE1), .sel(A1));
  Register #(.width(64)) reg5 (.D(or_41_out), .en(or_42_out), .Q(R5), .clk(clock_21_out));  // open: clr
  Clock clock_21 (.out(clock_21_out));
  Register #(.width(64)) reg21 (.D(or_43_out), .en(or_44_out), .Q(R21), .clk(clock_22_out));  // open: clr
  Clock clock_22 (.out(clock_22_out));
  Register #(.width(64)) reg37 (.D(or_45_out), .en(or_46_out), .Q(R37), .clk(clock_23_out));  // open: clr
  Clock clock_23 (.out(clock_23_out));
  Register #(.width(64)) reg53 (.D(or_47_out), .en(or_48_out), .Q(R53), .clk(clock_24_out));  // open: clr
  Clock clock_24 (.out(clock_24_out));
  assign or_49_out = A0R6 | A1R6;  // OR_Gate or_49, 64 bits wide
  or or_50 (or_50_out, A0L6, A1L6);
  assign or_51_out = A0R22 | A1R22;  // OR_Gate or_51, 64 bits wide
  or or_52 (or_52_out, A0L22, A1L22);
  assign or_53_out = A0R38 | A1R38;  // OR_Gate or_53, 64 bits wide
  or or_54 (or_54_out, A0L38, A1L38);
  assign or_55_out = A0R54 | A1R54;  // OR_Gate or_55, 64 bits wide
  or or_56 (or_56_out, A0L54, A1L54);
  Register #(.width(64)) reg6 (.D(or_49_out), .en(or_50_out), .Q(R6), .clk(clock_25_out));  // open: clr
  Clock clock_25 (.out(clock_25_out));
  Register #(.width(64)) reg22 (.D(or_51_out), .en(or_52_out), .Q(R22), .clk(clock_26_out));  // open: clr
  Clock clock_26 (.out(clock_26_out));
  Register #(.width(64)) reg38 (.D(or_53_out), .en(or_54_out), .Q(R38), .clk(clock_27_out));  // open: clr
  Clock clock_27 (.out(clock_27_out));
  Register #(.width(64)) reg54 (.D(or_55_out), .en(or_56_out), .Q(R54), .clk(clock_28_out));  // open: clr
  Clock clock_28 (.out(clock_28_out));
  assign or_57_out = A0R7 | A1R7;  // OR_Gate or_57, 64 bits wide
  or or_58 (or_58_out, A0L7, A1L7);
  assign or_59_out = A0R23 | A1R23;  // OR_Gate or_59, 64 bits wide
  or or_60 (or_60_out, A0L23, A1L23);
  assign or_61_out = A0R39 | A1R39;  // OR_Gate or_61, 64 bits wide
  or or_62 (or_62_out, A0L39, A1L39);
  assign or_63_out = A0R55 | A1R55;  // OR_Gate or_63, 64 bits wide
  or or_64 (or_64_out, A0L55, A1L55);
  Multiplexer #(.select(6), .width(64)) multiplexer_2 (
    .in0(R0), .in1(R1), .in2(R2), .in3(R3), .in4(R4), .in5(R5), .in6(R6), .in7(R7), .in8(R8), .in9(R9),
    .in10(R10), .in11(R11), .in12(R12), .in13(R13), .in14(R14), .in15(R15), .in16(R16), .in17(R17),
    .in18(R18), .in19(R19), .in20(R20), .in21(R21), .in22(R22), .in23(R23), .in24(R24), .in25(R25),
    .in26(R26), .in27(R27), .in28(R28), .in29(R29), .in30(R30), .in31(R31), .in32(R32), .in33(R33),
    .in34(R34), .in35(R35), .in36(R36), .in37(R37), .in38(R38), .in39(R39), .in40(R40), .in41(R41),
    .in42(R42), .in43(R43), .in44(R44), .in45(R45), .in46(R46), .in47(R47), .in48(R48), .in49(R49),
    .in50(R50), .in51(R51), .in52(R52), .in53(R53), .in54(R54), .in55(R55), .in56(R56), .in57(R57),
    .in58(R58), .in59(R59), .in60(R60), .in61(R61), .in62(R62), .in63(R63), .out(O1), .sel(A1));
  Register #(.width(64)) reg7 (.D(or_57_out), .en(or_58_out), .Q(R7), .clk(clock_29_out));  // open: clr
  Clock clock_29 (.out(clock_29_out));
  Register #(.width(64)) reg23 (.D(or_59_out), .en(or_60_out), .Q(R23), .clk(clock_30_out));  // open: clr
  Clock clock_30 (.out(clock_30_out));
  Register #(.width(64)) reg39 (.D(or_61_out), .en(or_62_out), .Q(R39), .clk(clock_31_out));  // open: clr
  Clock clock_31 (.out(clock_31_out));
  Register #(.width(64)) reg55 (.D(or_63_out), .en(or_64_out), .Q(R55), .clk(clock_32_out));  // open: clr
  Clock clock_32 (.out(clock_32_out));
  assign or_65_out = A0R8 | A1R8;  // OR_Gate or_65, 64 bits wide
  or or_66 (or_66_out, A0L8, A1L8);
  assign or_67_out = A0R24 | A1R24;  // OR_Gate or_67, 64 bits wide
  or or_68 (or_68_out, A0L24, A1L24);
  assign or_69_out = A0R40 | A1R40;  // OR_Gate or_69, 64 bits wide
  or or_70 (or_70_out, A0L40, A1L40);
  assign or_71_out = A0R56 | A1R56;  // OR_Gate or_71, 64 bits wide
  or or_72 (or_72_out, A0L56, A1L56);
  Register #(.width(64)) reg8 (.D(or_65_out), .en(or_66_out), .Q(R8), .clk(clock_33_out));  // open: clr
  Clock clock_33 (.out(clock_33_out));
  Register #(.width(64)) reg24 (.D(or_67_out), .en(or_68_out), .Q(R24), .clk(clock_34_out));  // open: clr
  Clock clock_34 (.out(clock_34_out));
  Register #(.width(64)) reg40 (.D(or_69_out), .en(or_70_out), .Q(R40), .clk(clock_35_out));  // open: clr
  Clock clock_35 (.out(clock_35_out));
  Register #(.width(64)) reg56 (.D(or_71_out), .en(or_72_out), .Q(R56), .clk(clock_36_out));  // open: clr
  Clock clock_36 (.out(clock_36_out));
  assign or_73_out = A0R9 | A1R9;  // OR_Gate or_73, 64 bits wide
  Register #(.width(64)) reg9 (.D(or_73_out), .en(or_74_out), .Q(R9), .clk(clock_37_out));  // open: clr
  or or_74 (or_74_out, A0L9, A1L9);
  Clock clock_37 (.out(clock_37_out));
  assign or_75_out = A0R25 | A1R25;  // OR_Gate or_75, 64 bits wide
  Register #(.width(64)) reg25 (.D(or_75_out), .en(or_76_out), .Q(R25), .clk(clock_38_out));  // open: clr
  or or_76 (or_76_out, A0L25, A1L25);
  Clock clock_38 (.out(clock_38_out));
  assign or_77_out = A0R41 | A1R41;  // OR_Gate or_77, 64 bits wide
  Register #(.width(64)) reg41 (.D(or_77_out), .en(or_78_out), .Q(R41), .clk(clock_39_out));  // open: clr
  or or_78 (or_78_out, A0L41, A1L41);
  Clock clock_39 (.out(clock_39_out));
  assign or_79_out = A0R57 | A1R57;  // OR_Gate or_79, 64 bits wide
  Register #(.width(64)) reg57 (.D(or_79_out), .en(or_80_out), .Q(R57), .clk(clock_40_out));  // open: clr
  or or_80 (or_80_out, A0L57, A1L57);
  Clock clock_40 (.out(clock_40_out));
  assign or_81_out = A0R10 | A1R10;  // OR_Gate or_81, 64 bits wide
  or or_82 (or_82_out, A0L10, A1L10);
  assign or_83_out = A0R26 | A1R26;  // OR_Gate or_83, 64 bits wide
  or or_84 (or_84_out, A0L26, A1L26);
  assign or_85_out = A0R42 | A1R42;  // OR_Gate or_85, 64 bits wide
  or or_86 (or_86_out, A0L42, A1L42);
  assign or_87_out = A0R58 | A1R58;  // OR_Gate or_87, 64 bits wide
  or or_88 (or_88_out, A0L58, A1L58);
  Register #(.width(64)) reg10 (.D(or_81_out), .en(or_82_out), .Q(R10), .clk(clock_41_out));  // open: clr
  Clock clock_41 (.out(clock_41_out));
  Register #(.width(64)) reg26 (.D(or_83_out), .en(or_84_out), .Q(R26), .clk(clock_42_out));  // open: clr
  Clock clock_42 (.out(clock_42_out));
  Register #(.width(64)) reg42 (.D(or_85_out), .en(or_86_out), .Q(R42), .clk(clock_43_out));  // open: clr
  Clock clock_43 (.out(clock_43_out));
  Register #(.width(64)) reg58 (.D(or_87_out), .en(or_88_out), .Q(R58), .clk(clock_44_out));  // open: clr
  Clock clock_44 (.out(clock_44_out));
  assign or_89_out = A0R11 | A1R11;  // OR_Gate or_89, 64 bits wide
  Register #(.width(64)) reg11 (.D(or_89_out), .en(or_90_out), .Q(R11), .clk(clock_45_out));  // open: clr
  or or_90 (or_90_out, A0L11, A1L11);
  Clock clock_45 (.out(clock_45_out));
  assign or_91_out = A0R27 | A1R27;  // OR_Gate or_91, 64 bits wide
  Register #(.width(64)) reg27 (.D(or_91_out), .en(or_92_out), .Q(R27), .clk(clock_46_out));  // open: clr
  or or_92 (or_92_out, A0L27, A1L27);
  Clock clock_46 (.out(clock_46_out));
  assign or_93_out = A0R43 | A1R43;  // OR_Gate or_93, 64 bits wide
  Register #(.width(64)) reg43 (.D(or_93_out), .en(or_94_out), .Q(R43), .clk(clock_47_out));  // open: clr
  or or_94 (or_94_out, A0L43, A1L43);
  Clock clock_47 (.out(clock_47_out));
  assign or_95_out = A0R59 | A1R59;  // OR_Gate or_95, 64 bits wide
  Register #(.width(64)) reg59 (.D(or_95_out), .en(or_96_out), .Q(R59), .clk(clock_48_out));  // open: clr
  or or_96 (or_96_out, A0L59, A1L59);
  Clock clock_48 (.out(clock_48_out));
  assign or_97_out = A0R12 | A1R12;  // OR_Gate or_97, 64 bits wide
  Register #(.width(64)) reg12 (.D(or_97_out), .en(or_98_out), .Q(R12), .clk(clock_49_out));  // open: clr
  or or_98 (or_98_out, A0L12, A1L12);
  Clock clock_49 (.out(clock_49_out));
  assign or_99_out = A0R28 | A1R28;  // OR_Gate or_99, 64 bits wide
  Register #(.width(64)) reg28 (.D(or_99_out), .en(or_100_out), .Q(R28), .clk(clock_50_out));  // open: clr
  or or_100 (or_100_out, A0L28, A1L28);
  Clock clock_50 (.out(clock_50_out));
  assign or_101_out = A0R44 | A1R44;  // OR_Gate or_101, 64 bits wide
  Register #(.width(64)) reg44 (.D(or_101_out), .en(or_102_out), .Q(R44), .clk(clock_51_out));  // open: clr
  or or_102 (or_102_out, A0L44, A1L44);
  Clock clock_51 (.out(clock_51_out));
  assign or_103_out = A0R60 | A1R60;  // OR_Gate or_103, 64 bits wide
  Register #(.width(64)) reg60 (.D(or_103_out), .en(or_104_out), .Q(R60), .clk(clock_52_out));  // open: clr
  or or_104 (or_104_out, A0L60, A1L60);
  Clock clock_52 (.out(clock_52_out));
  assign or_105_out = A0R13 | A1R13;  // OR_Gate or_105, 64 bits wide
  or or_106 (or_106_out, A0L13, A1L13);
  Clock clock_53 (.out(clock_53_out));
  assign or_107_out = A0R29 | A1R29;  // OR_Gate or_107, 64 bits wide
  or or_108 (or_108_out, A0L29, A1L29);
  Clock clock_54 (.out(clock_54_out));
  assign or_109_out = A0R45 | A1R45;  // OR_Gate or_109, 64 bits wide
  or or_110 (or_110_out, A0L45, A1L45);
  Clock clock_55 (.out(clock_55_out));
  assign or_111_out = A0R61 | A1R61;  // OR_Gate or_111, 64 bits wide
  or or_112 (or_112_out, A0L61, A1L61);
  Clock clock_56 (.out(clock_56_out));
  Register #(.width(64)) reg13 (.D(or_105_out), .en(or_106_out), .Q(R13), .clk(clock_53_out));  // open: clr
  Register #(.width(64)) reg29 (.D(or_107_out), .en(or_108_out), .Q(R29), .clk(clock_54_out));  // open: clr
  Register #(.width(64)) reg45 (.D(or_109_out), .en(or_110_out), .Q(R45), .clk(clock_55_out));  // open: clr
  Register #(.width(64)) reg61 (.D(or_111_out), .en(or_112_out), .Q(R61), .clk(clock_56_out));  // open: clr
  assign or_113_out = A0R14 | A1R14;  // OR_Gate or_113, 64 bits wide
  Register #(.width(64)) reg14 (.D(or_113_out), .en(or_114_out), .Q(R14), .clk(clock_57_out));  // open: clr
  or or_114 (or_114_out, A0L14, A1L14);
  Clock clock_57 (.out(clock_57_out));
  assign or_115_out = A0R30 | A1R30;  // OR_Gate or_115, 64 bits wide
  Register #(.width(64)) reg30 (.D(or_115_out), .en(or_116_out), .Q(R30), .clk(clock_58_out));  // open: clr
  or or_116 (or_116_out, A0L30, A1L30);
  Clock clock_58 (.out(clock_58_out));
  assign or_117_out = A0R46 | A1R46;  // OR_Gate or_117, 64 bits wide
  Register #(.width(64)) reg46 (.D(or_117_out), .en(or_118_out), .Q(R46), .clk(clock_59_out));  // open: clr
  or or_118 (or_118_out, A0L46, A1L46);
  Clock clock_59 (.out(clock_59_out));
  assign or_119_out = A0R62 | A1R62;  // OR_Gate or_119, 64 bits wide
  Register #(.width(64)) reg62 (.D(or_119_out), .en(or_120_out), .Q(R62), .clk(clock_60_out));  // open: clr
  or or_120 (or_120_out, A0L62, A1L62);
  Clock clock_60 (.out(clock_60_out));
  assign or_121_out = A0R15 | A1R15;  // OR_Gate or_121, 64 bits wide
  or or_122 (or_122_out, A0L15, A1L15);
  Clock clock_61 (.out(clock_61_out));
  assign or_123_out = A0R31 | A1R31;  // OR_Gate or_123, 64 bits wide
  or or_124 (or_124_out, A0L31, A1L31);
  Clock clock_62 (.out(clock_62_out));
  assign or_125_out = A0R47 | A1R47;  // OR_Gate or_125, 64 bits wide
  or or_126 (or_126_out, A0L47, A1L47);
  Clock clock_63 (.out(clock_63_out));
  assign or_127_out = A0R63 | A1R63;  // OR_Gate or_127, 64 bits wide
  or or_128 (or_128_out, A0L63, A1L63);
  Clock clock_64 (.out(clock_64_out));
  Register #(.width(64)) reg15 (.D(or_121_out), .en(or_122_out), .Q(R15), .clk(clock_61_out));  // open: clr
  Register #(.width(64)) reg31 (.D(or_123_out), .en(or_124_out), .Q(R31), .clk(clock_62_out));  // open: clr
  Register #(.width(64)) reg47 (.D(or_125_out), .en(or_126_out), .Q(R47), .clk(clock_63_out));  // open: clr
  Register #(.width(64)) reg63 (.D(or_127_out), .en(or_128_out), .Q(R63), .clk(clock_64_out));  // open: clr
endmodule
