// Logisim project muxrisccore.circ as structural Verilog: 4 circuits, main circuit main
module main (
);

  wire clock_1_out;
  wire [16:0] bitselector_1_out;
  wire [63:0] chip_1_output1, ram_1_dout;

  RAM #(.addrWidth(17), .dataWidth(64), .trigger("falling"), .\type ("nonvolatile")) ram_1 (
    .addr(bitselector_1_out), .clk(clock_1_out), .dout(ram_1_dout));  // open: we, oe, din
  BitSelector #(.group(17), .width(64)) bitselector_1 (.in(chip_1_output1), .out(bitselector_1_out), .sel(2'b00));
  Clock clock_1 (.out(clock_1_out));
  chip chip_1 (
    .input1(ram_1_dout), .output1(chip_1_output1));  // open: input2, input3, input4, input5, input6, input7, input8, input9, input10, input11, input12, input13, input14, input15, input16, output2, output3, output4, output5, output6, output7, output8, output9, output10, output11, output12, output13, output14, output15, output16
endmodule

module registry (
  input  [63:0] value,
  input  update,
  input  [15:0] regX,
  input  [15:0] regY,
  input  [15:0] regZ,
  input  [63:0] coreout0,
  input  [63:0] clockin0,
  input  [63:0] freqin0,
  input  [63:0] input0,
  input  [63:0] input1r,
  input  [63:0] input2r,
  input  [63:0] input3r,
  input  [63:0] input4r,
  input  [63:0] input5r,
  input  [63:0] input6r,
  input  [63:0] input7r,
  input  [63:0] input8r,
  input  [63:0] input9r,
  input  [63:0] input10r,
  input  [63:0] input11r,
  input  [63:0] input12r,
  input  [63:0] input13r,
  input  [63:0] input14r,
  input  [63:0] input15r,
  input  [63:0] input16r,
  input  [63:0] input1d,
  input  [63:0] input2d,
  input  [63:0] input3d,
  input  [63:0] input4d,
  input  [63:0] input5d,
  input  [63:0] input6d,
  input  [63:0] input7d,
  input  [63:0] input8d,
  input  [63:0] input9d,
  input  [63:0] input10d,
  input  [63:0] input11d,
  input  [63:0] input12d,
  input  [63:0] input13d,
  input  [63:0] input14d,
  input  [63:0] input15d,
  input  [63:0] input16d,
  output [63:0] regXout,
  output [63:0] regYout,
  output [63:0] regZout,
  output [63:0] corein0,
  output [63:0] clockout0,
  output [63:0] freqout0,
  output [63:0] output0,
  output [63:0] output1r,
  output [63:0] output2r,
  output [63:0] output3r,
  output [63:0] output4r,
  output [63:0] output5r,
  output [63:0] output6r,
  output [63:0] output7r,
  output [63:0] output8r,
  output [63:0] output9r,
  output [63:0] output10r,
  output [63:0] output11r,
  output [63:0] output12r,
  output [63:0] output13r,
  output [63:0] output14r,
  output [63:0] output15r,
  output [63:0] output16r,
  output [63:0] output1d,
  output [63:0] output2d,
  output [63:0] output3d,
  output [63:0] output4d,
  output [63:0] output5d,
  output [63:0] output6d,
  output [63:0] output7d,
  output [63:0] output8d,
  output [63:0] output9d,
  output [63:0] output10d,
  output [63:0] output11d,
  output [63:0] output12d,
  output [63:0] output13d,
  output [63:0] output14d,
  output [63:0] output15d,
  output [63:0] output16d
);

  wire clock_1_out, clock_2_out, clock_3_out, clock_4_out, clock_5_out, clock_6_out, clock_7_out,
       clock_8_out, clock_9_out, clock_10_out, clock_11_out, clock_12_out, clock_13_out, clock_14_out,
       clock_15_out, clock_16_out, clock_17_out, clock_18_out, clock_19_out, clock_20_out, clock_21_out,
       clock_22_out, clock_23_out, clock_24_out, clock_25_out, clock_26_out, clock_27_out, clock_28_out,
       clock_29_out, clock_30_out, clock_31_out, clock_32_out, clock_33_out, clock_34_out, clock_35_out,
       clock_36_out, clock_37_out, clock_38_out, clock_39_out, clock_40_out, clock_41_out, clock_42_out,
       clock_43_out, clock_44_out, clock_45_out, clock_46_out, clock_47_out, clock_48_out, clock_49_out,
       clock_50_out, clock_51_out, clock_52_out, clock_53_out, clock_54_out, clock_55_out, clock_56_out,
       clock_57_out, clock_58_out, clock_59_out, clock_60_out, clock_61_out, clock_62_out, clock_63_out,
       clock_64_out, clock_65_out, clock_66_out, clock_67_out, clock_68_out, clock_69_out, clock_70_out,
       clock_71_out, clock_72_out, clock_73_out, clock_74_out, clock_75_out, clock_76_out, clock_77_out,
       clock_78_out, clock_79_out, clock_80_out, clock_81_out, clock_82_out, clock_83_out, clock_84_out,
       clock_85_out, clock_86_out, clock_87_out, clock_88_out, clock_89_out, clock_90_out, clock_91_out,
       clock_92_out, clock_93_out, clock_94_out, clock_95_out, clock_96_out, clock_97_out, clock_98_out,
       clock_99_out, clock_100_out, clock_101_out, clock_102_out, clock_103_out, clock_104_out,
       clock_105_out, clock_106_out, clock_107_out, clock_108_out, clock_109_out, clock_110_out,
       clock_111_out, clock_112_out, clock_113_out, clock_114_out, clock_115_out, clock_116_out,
       clock_117_out, clock_118_out, clock_119_out, clock_120_out, clock_121_out, clock_122_out,
       clock_123_out, clock_124_out, clock_125_out, clock_126_out, clock_127_out, clock_128_out,
       clock_129_out, clock_130_out, clock_131_out, clock_132_out, clock_133_out, clock_134_out,
       clock_135_out, clock_136_out, clock_137_out, clock_138_out, clock_139_out, clock_140_out,
       clock_141_out, clock_142_out, clock_143_out, clock_144_out, clock_145_out, clock_146_out,
       clock_147_out, clock_148_out, clock_149_out, clock_150_out, clock_151_out, clock_152_out,
       clock_153_out, clock_154_out, clock_155_out, clock_156_out, clock_157_out, clock_158_out,
       clock_159_out, clock_160_out, clock_161_out, clock_162_out, clock_163_out, clock_164_out,
       clock_165_out, clock_166_out, clock_167_out, clock_168_out, clock_169_out, clock_170_out,
       clock_171_out, clock_172_out, clock_173_out, clock_174_out, clock_175_out, clock_176_out,
       clock_177_out, clock_178_out, clock_179_out, clock_180_out, clock_181_out, clock_182_out,
       clock_183_out, clock_184_out, clock_185_out, clock_186_out, clock_187_out, clock_188_out,
       clock_189_out, clock_190_out, clock_191_out, clock_192_out, clock_193_out, clock_194_out,
       clock_195_out, clock_196_out, clock_197_out, clock_198_out, clock_199_out, clock_200_out,
       clock_201_out, clock_202_out, clock_203_out, clock_204_out, clock_205_out, clock_206_out,
       clock_207_out, clock_208_out, clock_209_out, clock_210_out, clock_211_out, clock_212_out,
       clock_213_out, clock_214_out, clock_215_out, clock_216_out, clock_217_out, clock_218_out,
       clock_219_out, clock_220_out, clock_221_out, clock_222_out, clock_223_out, clock_224_out,
       clock_225_out, clock_226_out, clock_227_out, clock_228_out, clock_229_out, clock_230_out,
       clock_231_out, clock_232_out, clock_233_out, clock_234_out, clock_235_out, clock_236_out,
       clock_237_out, clock_238_out, clock_239_out, clock_240_out, clock_241_out, clock_242_out,
       clock_243_out, clock_244_out, clock_245_out, clock_246_out, clock_247_out, clock_248_out,
       clock_249_out, clock_250_out, clock_251_out, clock_252_out, clock_253_out, clock_254_out,
       clock_255_out, clock_256_out, u1, u2, u3, u4, u5, u6, u7, u8, u9, u10, u11, u12, u13, u14, u15, u16,
       u17, u18, u19, u20, u21, u22, u23, u24, u25, u26, u27, u28, u29, u30, u31, u32, u33, u34, u35, u36,
       u37, u38, u39, u40, u41, u42, u43, u44, u45, u46, u47, u48, u49, u50, u51, u52, u53, u54, u55, u56,
       u57, u58, u59, u60, u61, u62, u63, u64, u65, u66, u67, u68, u69, u70, u71, u72, u73, u74, u75, u76,
       u77, u78, u79, u80, u81, u82, u83, u84, u85, u86, u87, u88, u89, u90, u91, u92, u93, u94, u95, u96,
       u97, u98, u99, u100, u101, u102, u103, u104, u105, u106, u107, u108, u109, u110, u111, u112, u113,
       u114, u115, u116, u117, u118, u119, u120, u121, u122, u123, u124, u125, u126, u127, u128, u129, u130,
       u131, u132, u133, u134, u135, u136, u137, u138, u139, u140, u141, u142, u143, u144, u145, u146, u147,
       u148, u149, u150, u151, u152, u153, u154, u155, u156, u157, u158, u159, u160, u161, u162, u163, u164,
       u165, u166, u167, u168, u169, u170, u171, u172, u173, u174, u175, u176, u177, u178, u179, u180, u181,
       u182, u183, u184, u185, u186, u187, u188, u189, u190, u191, u192, u193, u194, u195, u196, u197, u198,
       u199, u200, u201, u202, u203, u204, u205, u206, u207, u208, u209, u210, u211, u212, u213, u214, u215,
       u216, u217, u218, u219, u220, u221, u222, u223, u224, u225, u226, u227, u228, u229, u230, u231, u232,
       u233, u234, u235, u236, u237, u238, u239, u240, u241, u242, u243, u244, u245, u246, u247, u248, u249,
       u250, u251, u252, u253, u254, u255, u256;
  wire [7:0] regX_t, regY_t, regZ_t;
  wire [63:0] v1, v2, v3, v4, v5, v6, v7, v8, v9, v10, v11, v12, v13, v14, v15, v16, v17, v18, v19, v20, v21,
       v22, v23, v24, v25, v26, v27, v28, v29, v30, v31, v32, v33, v34, v35, v36, v37, v38, v39, v40, v41,
       v42, v43, v44, v45, v46, v47, v48, v49, v50, v51, v52, v53, v54, v55, v56, v57, v58, v59, v60, v61,
       v62, v63, v64, v65, v66, v67, v68, v69, v70, v71, v72, v73, v74, v75, v76, v77, v78, v79, v80, v81,
       v82, v83, v84, v85, v86, v87, v88, v89, v90, v91, v92, v93, v94, v95, v96, v97, v98, v99, v100, v101,
       v102, v103, v104, v105, v106, v107, v108, v109, v110, v111, v112, v113, v114, v115, v116, v117, v118,
       v119, v120, v121, v122, v123, v124, v125, v126, v127, v128, v129, v130, v131, v132, v133, v134, v135,
       v136, v137, v138, v139, v140, v141, v142, v143, v144, v145, v146, v147, v148, v149, v150, v151, v152,
       v153, v154, v155, v156, v157, v158, v159, v160, v161, v162, v163, v164, v165, v166, v167, v168, v169,
       v170, v171, v172, v173, v174, v175, v176, v177, v178, v179, v180, v181, v182, v183, v184, v185, v186,
       v187, v188, v189, v190, v191, v192, v193, v194, v195, v196, v197, v198, v199, v200, v201, v202, v203,
       v204, v205, v206, v207, v208, v209, v210, v211, v212, v213, v214, v215, v216, v217, v218, v219, v220;

  Demultiplexer #(.select(8)) demultiplexer_1 (
    .out0(u1), .out1(u2), .out2(u3), .out3(u4), .out4(u5), .out5(u6), .out6(u7), .out7(u8), .out8(u9),
    .out9(u10), .out10(u11), .out11(u12), .out12(u13), .out13(u14), .out14(u15), .out15(u16), .out16(u17),
    .out17(u18), .out18(u19), .out19(u20), .out20(u21), .out21(u22), .out22(u23), .out23(u24), .out24(u25),
    .out25(u26), .out26(u27), .out27(u28), .out28(u29), .out29(u30), .out30(u31), .out31(u32), .out32(u33),
    .out33(u34), .out34(u35), .out35(u36), .out36(u37), .out37(u38), .out38(u39), .out39(u40), .out40(u41),
    .out41(u42), .out42(u43), .out43(u44), .out44(u45), .out45(u46), .out46(u47), .out47(u48), .out48(u49),
    .out49(u50), .out50(u51), .out51(u52), .out52(u53), .out53(u54), .out54(u55), .out55(u56), .out56(u57),
    .out57(u58), .out58(u59), .out59(u60), .out60(u61), .out61(u62), .out62(u63), .out63(u64), .out64(u65),
    .out65(u66), .out66(u67), .out67(u68), .out68(u69), .out69(u70), .out70(u71), .out71(u72), .out72(u73),
    .out73(u74), .out74(u75), .out75(u76), .out76(u77), .out77(u78), .out78(u79), .out79(u80), .out80(u81),
    .out81(u82), .out82(u83), .out83(u84), .out84(u85), .out85(u86), .out86(u87), .out87(u88), .out88(u89),
    .out89(u90), .out90(u91), .out91(u92), .out92(u93), .out93(u94), .out94(u95), .out95(u96), .out96(u97),
    .out97(u98), .out98(u99), .out99(u100), .out100(u101), .out101(u102), .out102(u103), .out103(u104),
    .out104(u105), .out105(u106), .out106(u107), .out107(u108), .out108(u109), .out109(u110), .out110(u111),
    .out111(u112), .out112(u113), .out113(u114), .out114(u115), .out115(u116), .out116(u117), .out117(u118),
    .out118(u119), .out119(u120), .out120(u121), .out121(u122), .out122(u123), .out123(u124), .out124(u125),
    .out125(u126), .out126(u127), .out127(u128), .out128(u129), .out129(u130), .out130(u131), .out131(u132),
    .out132(u133), .out133(u134), .out134(u135), .out135(u136), .out136(u137), .out137(u138), .out138(u139),
    .out139(u140), .out140(u141), .out141(u142), .out142(u143), .out143(u144), .out144(u145), .out145(u146),
    .out146(u147), .out147(u148), .out148(u149), .out149(u150), .out150(u151), .out151(u152), .out152(u153),
    .out153(u154), .out154(u155), .out155(u156), .out156(u157), .out157(u158), .out158(u159), .out159(u160),
    .out160(u161), .out161(u162), .out162(u163), .out163(u164), .out164(u165), .out165(u166), .out166(u167),
    .out167(u168), .out168(u169), .out169(u170), .out170(u171), .out171(u172), .out172(u173), .out173(u174),
    .out174(u175), .out175(u176), .out176(u177), .out177(u178), .out178(u179), .out179(u180), .out180(u181),
    .out181(u182), .out182(u183), .out183(u184), .out184(u185), .out185(u186), .out186(u187), .out187(u188),
    .out188(u189), .out189(u190), .out190(u191), .out191(u192), .out192(u193), .out193(u194), .out194(u195),
    .out195(u196), .out196(u197), .out197(u198), .out198(u199), .out199(u200), .out200(u201), .out201(u202),
    .out202(u203), .out203(u204), .out204(u205), .out205(u206), .out206(u207), .out207(u208), .out208(u209),
    .out209(u210), .out210(u211), .out211(u212), .out212(u213), .out213(u214), .out214(u215), .out215(u216),
    .out216(u217), .out217(u218), .out218(u219), .out219(u220), .out220(u221), .out221(u222), .out222(u223),
    .out223(u224), .out224(u225), .out225(u226), .out226(u227), .out227(u228), .out228(u229), .out229(u230),
    .out230(u231), .out231(u232), .out232(u233), .out233(u234), .out234(u235), .out235(u236), .out236(u237),
    .out237(u238), .out238(u239), .out239(u240), .out240(u241), .out241(u242), .out242(u243), .out243(u244),
    .out244(u245), .out245(u246), .out246(u247), .out247(u248), .out248(u249), .out249(u250), .out250(u251),
    .out251(u252), .out252(u253), .out253(u254), .out254(u255), .out255(u256), .in(update), .sel(regX_t));
  BitSelector #(.group(8), .width(16)) bitselector_1 (.in(regX), .out(regX_t), .sel(1'b0));
  BitSelector #(.group(8), .width(16)) bitselector_2 (.in(regY), .out(regY_t), .sel(1'b0));
  BitSelector #(.group(8), .width(16)) bitselector_3 (.in(regZ), .out(regZ_t), .sel(1'b0));
  Register #(.width(64)) register_1 (.D(value), .en(u1), .clk(clock_1_out), .Q(v1));  // open: clr
  Clock clock_1 (.out(clock_1_out));
  Register #(.width(64)) register_2 (.D(value), .en(u9), .clk(clock_2_out), .Q(v9));  // open: clr
  Clock clock_2 (.out(clock_2_out));
  Register #(.width(64)) register_3 (.D(value), .en(u17), .clk(clock_3_out), .Q(v17));  // open: clr
  Clock clock_3 (.out(clock_3_out));
  Register #(.width(64)) register_4 (.D(value), .en(u25), .clk(clock_4_out), .Q(v25));  // open: clr
  Clock clock_4 (.out(clock_4_out));
  Register #(.width(64)) register_5 (.D(value), .en(u33), .clk(clock_5_out), .Q(v33));  // open: clr
  Clock clock_5 (.out(clock_5_out));
  Register #(.width(64)) register_6 (.D(value), .en(u41), .clk(clock_6_out), .Q(v41));  // open: clr
  Clock clock_6 (.out(clock_6_out));
  Register #(.width(64)) register_7 (.D(value), .en(u49), .clk(clock_7_out), .Q(v49));  // open: clr
  Clock clock_7 (.out(clock_7_out));
  Register #(.width(64)) register_8 (.D(value), .en(u57), .clk(clock_8_out), .Q(v57));  // open: clr
  Clock clock_8 (.out(clock_8_out));
  Register #(.width(64)) register_9 (.D(value), .en(u65), .clk(clock_9_out), .Q(v65));  // open: clr
  Clock clock_9 (.out(clock_9_out));
  Register #(.width(64)) register_10 (.D(value), .en(u73), .clk(clock_10_out), .Q(v73));  // open: clr
  Clock clock_10 (.out(clock_10_out));
  Register #(.width(64)) register_11 (.D(value), .en(u81), .clk(clock_11_out), .Q(v81));  // open: clr
  Clock clock_11 (.out(clock_11_out));
  Register #(.width(64)) register_12 (.D(value), .en(u89), .clk(clock_12_out), .Q(v89));  // open: clr
  Clock clock_12 (.out(clock_12_out));
  Register #(.width(64)) register_13 (.D(value), .en(u97), .clk(clock_13_out), .Q(v97));  // open: clr
  Clock clock_13 (.out(clock_13_out));
  Register #(.width(64)) register_14 (.D(value), .en(u105), .clk(clock_14_out), .Q(v105));  // open: clr
  Clock clock_14 (.out(clock_14_out));
  Register #(.width(64)) register_15 (.D(value), .en(u113), .clk(clock_15_out), .Q(v113));  // open: clr
  Clock clock_15 (.out(clock_15_out));
  Register #(.width(64)) register_16 (.D(value), .en(u121), .clk(clock_16_out), .Q(v121));  // open: clr
  Clock clock_16 (.out(clock_16_out));
  Register #(.width(64)) register_17 (.D(value), .en(u129), .clk(clock_17_out), .Q(v129));  // open: clr
  Clock clock_17 (.out(clock_17_out));
  Register #(.width(64)) register_18 (.D(value), .en(u137), .clk(clock_18_out), .Q(v137));  // open: clr
  Clock clock_18 (.out(clock_18_out));
  Register #(.width(64)) register_19 (.D(value), .en(u145), .clk(clock_19_out), .Q(v145));  // open: clr
  Clock clock_19 (.out(clock_19_out));
  Register #(.width(64)) register_20 (.D(value), .en(u153), .clk(clock_20_out), .Q(v153));  // open: clr
  Clock clock_20 (.out(clock_20_out));
  Register #(.width(64)) register_21 (.D(value), .en(u161), .clk(clock_21_out), .Q(v161));  // open: clr
  Clock clock_21 (.out(clock_21_out));
  Register #(.width(64)) register_22 (.D(value), .en(u169), .clk(clock_22_out), .Q(v169));  // open: clr
  Clock clock_22 (.out(clock_22_out));
  Register #(.width(64)) register_23 (.D(value), .en(u177), .clk(clock_23_out), .Q(v177));  // open: clr
  Clock clock_23 (.out(clock_23_out));
  Register #(.width(64)) register_24 (.D(value), .en(u185), .clk(clock_24_out), .Q(v185));  // open: clr
  Clock clock_24 (.out(clock_24_out));
  Register #(.width(64)) register_25 (.D(value), .en(u193), .clk(clock_25_out), .Q(v193));  // open: clr
  Clock clock_25 (.out(clock_25_out));
  Register #(.width(64)) register_26 (.D(value), .en(u201), .clk(clock_26_out), .Q(v201));  // open: clr
  Clock clock_26 (.out(clock_26_out));
  Register #(.width(64)) register_27 (.D(value), .en(u209), .clk(clock_27_out), .Q(v209));  // open: clr
  Clock clock_27 (.out(clock_27_out));
  Register #(.width(64)) register_28 (.D(value), .en(u217), .clk(clock_28_out), .Q(v217));  // open: clr
  Clock clock_28 (.out(clock_28_out));
  Register #(.width(64)) register_29 (.D(value), .en(u2), .clk(clock_29_out), .Q(v2));  // open: clr
  Clock clock_29 (.out(clock_29_out));
  Register #(.width(64)) register_30 (.D(value), .en(u10), .clk(clock_30_out), .Q(v10));  // open: clr
  Clock clock_30 (.out(clock_30_out));
  Register #(.width(64)) register_31 (.D(value), .en(u18), .clk(clock_31_out), .Q(v18));  // open: clr
  Clock clock_31 (.out(clock_31_out));
  Register #(.width(64)) register_32 (.D(value), .en(u26), .clk(clock_32_out), .Q(v26));  // open: clr
  Clock clock_32 (.out(clock_32_out));
  Register #(.width(64)) register_33 (.D(value), .en(u34), .clk(clock_33_out), .Q(v34));  // open: clr
  Clock clock_33 (.out(clock_33_out));
  Register #(.width(64)) register_34 (.D(value), .en(u42), .clk(clock_34_out), .Q(v42));  // open: clr
  Clock clock_34 (.out(clock_34_out));
  Register #(.width(64)) register_35 (.D(value), .en(u50), .clk(clock_35_out), .Q(v50));  // open: clr
  Clock clock_35 (.out(clock_35_out));
  Register #(.width(64)) register_36 (.D(value), .en(u58), .clk(clock_36_out), .Q(v58));  // open: clr
  Clock clock_36 (.out(clock_36_out));
  Register #(.width(64)) register_37 (.D(value), .en(u66), .clk(clock_37_out), .Q(v66));  // open: clr
  Clock clock_37 (.out(clock_37_out));
  Register #(.width(64)) register_38 (.D(value), .en(u74), .clk(clock_38_out), .Q(v74));  // open: clr
  Clock clock_38 (.out(clock_38_out));
  Register #(.width(64)) register_39 (.D(value), .en(u82), .clk(clock_39_out), .Q(v82));  // open: clr
  Clock clock_39 (.out(clock_39_out));
  Register #(.width(64)) register_40 (.D(value), .en(u90), .clk(clock_40_out), .Q(v90));  // open: clr
  Clock clock_40 (.out(clock_40_out));
  Register #(.width(64)) register_41 (.D(value), .en(u98), .clk(clock_41_out), .Q(v98));  // open: clr
  Clock clock_41 (.out(clock_41_out));
  Register #(.width(64)) register_42 (.D(value), .en(u106), .clk(clock_42_out), .Q(v106));  // open: clr
  Clock clock_42 (.out(clock_42_out));
  Register #(.width(64)) register_43 (.D(value), .en(u114), .clk(clock_43_out), .Q(v114));  // open: clr
  Clock clock_43 (.out(clock_43_out));
  Register #(.width(64)) register_44 (.D(value), .en(u122), .clk(clock_44_out), .Q(v122));  // open: clr
  Clock clock_44 (.out(clock_44_out));
  Register #(.width(64)) register_45 (.D(value), .en(u130), .clk(clock_45_out), .Q(v130));  // open: clr
  Clock clock_45 (.out(clock_45_out));
  Register #(.width(64)) register_46 (.D(value), .en(u138), .clk(clock_46_out), .Q(v138));  // open: clr
  Clock clock_46 (.out(clock_46_out));
  Register #(.width(64)) register_47 (.D(value), .en(u146), .clk(clock_47_out), .Q(v146));  // open: clr
  Clock clock_47 (.out(clock_47_out));
  Register #(.width(64)) register_48 (.D(value), .en(u154), .clk(clock_48_out), .Q(v154));  // open: clr
  Clock clock_48 (.out(clock_48_out));
  Register #(.width(64)) register_49 (.D(value), .en(u162), .clk(clock_49_out), .Q(v162));  // open: clr
  Clock clock_49 (.out(clock_49_out));
  Register #(.width(64)) register_50 (.D(value), .en(u170), .clk(clock_50_out), .Q(v170));  // open: clr
  Clock clock_50 (.out(clock_50_out));
  Register #(.width(64)) register_51 (.D(value), .en(u178), .clk(clock_51_out), .Q(v178));  // open: clr
  Clock clock_51 (.out(clock_51_out));
  Register #(.width(64)) register_52 (.D(value), .en(u186), .clk(clock_52_out), .Q(v186));  // open: clr
  Clock clock_52 (.out(clock_52_out));
  Register #(.width(64)) register_53 (.D(value), .en(u194), .clk(clock_53_out), .Q(v194));  // open: clr
  Clock clock_53 (.out(clock_53_out));
  Register #(.width(64)) register_54 (.D(value), .en(u202), .clk(clock_54_out), .Q(v202));  // open: clr
  Clock clock_54 (.out(clock_54_out));
  Register #(.width(64)) register_55 (.D(value), .en(u210), .clk(clock_55_out), .Q(v210));  // open: clr
  Clock clock_55 (.out(clock_55_out));
  Register #(.width(64)) register_56 (.D(value), .en(u218), .clk(clock_56_out), .Q(v218));  // open: clr
  Clock clock_56 (.out(clock_56_out));
  Register #(.width(64)) register_57 (.D(value), .en(u3), .clk(clock_57_out), .Q(v3));  // open: clr
  Clock clock_57 (.out(clock_57_out));
  Register #(.width(64)) register_58 (.D(value), .en(u11), .clk(clock_58_out), .Q(v11));  // open: clr
  Clock clock_58 (.out(clock_58_out));
  Register #(.width(64)) register_59 (.D(value), .en(u19), .clk(clock_59_out), .Q(v19));  // open: clr
  Clock clock_59 (.out(clock_59_out));
  Register #(.width(64)) register_60 (.D(value), .en(u27), .clk(clock_60_out), .Q(v27));  // open: clr
  Clock clock_60 (.out(clock_60_out));
  Register #(.width(64)) register_61 (.D(value), .en(u35), .clk(clock_61_out), .Q(v35));  // open: clr
  Clock clock_61 (.out(clock_61_out));
  Register #(.width(64)) register_62 (.D(value), .en(u43), .clk(clock_62_out), .Q(v43));  // open: clr
  Clock clock_62 (.out(clock_62_out));
  Register #(.width(64)) register_63 (.D(value), .en(u51), .clk(clock_63_out), .Q(v51));  // open: clr
  Clock clock_63 (.out(clock_63_out));
  Register #(.width(64)) register_64 (.D(value), .en(u59), .clk(clock_64_out), .Q(v59));  // open: clr
  Clock clock_64 (.out(clock_64_out));
  Register #(.width(64)) register_65 (.D(value), .en(u67), .clk(clock_65_out), .Q(v67));  // open: clr
  Clock clock_65 (.out(clock_65_out));
  Register #(.width(64)) register_66 (.D(value), .en(u75), .clk(clock_66_out), .Q(v75));  // open: clr
  Clock clock_66 (.out(clock_66_out));
  Register #(.width(64)) register_67 (.D(value), .en(u83), .clk(clock_67_out), .Q(v83));  // open: clr
  Clock clock_67 (.out(clock_67_out));
  Register #(.width(64)) register_68 (.D(value), .en(u91), .clk(clock_68_out), .Q(v91));  // open: clr
  Clock clock_68 (.out(clock_68_out));
  Register #(.width(64)) register_69 (.D(value), .en(u99), .clk(clock_69_out), .Q(v99));  // open: clr
  Clock clock_69 (.out(clock_69_out));
  Register #(.width(64)) register_70 (.D(value), .en(u107), .clk(clock_70_out), .Q(v107));  // open: clr
  Clock clock_70 (.out(clock_70_out));
  Register #(.width(64)) register_71 (.D(value), .en(u115), .clk(clock_71_out), .Q(v115));  // open: clr
  Clock clock_71 (.out(clock_71_out));
  Register #(.width(64)) register_72 (.D(value), .en(u123), .clk(clock_72_out), .Q(v123));  // open: clr
  Clock clock_72 (.out(clock_72_out));
  Register #(.width(64)) register_73 (.D(value), .en(u131), .clk(clock_73_out), .Q(v131));  // open: clr
  Clock clock_73 (.out(clock_73_out));
  Register #(.width(64)) register_74 (.D(value), .en(u139), .clk(clock_74_out), .Q(v139));  // open: clr
  Clock clock_74 (.out(clock_74_out));
  Register #(.width(64)) register_75 (.D(value), .en(u147), .clk(clock_75_out), .Q(v147));  // open: clr
  Clock clock_75 (.out(clock_75_out));
  Register #(.width(64)) register_76 (.D(value), .en(u155), .clk(clock_76_out), .Q(v155));  // open: clr
  Clock clock_76 (.out(clock_76_out));
  Register #(.width(64)) register_77 (.D(value), .en(u163), .clk(clock_77_out), .Q(v163));  // open: clr
  Clock clock_77 (.out(clock_77_out));
  Register #(.width(64)) register_78 (.D(value), .en(u171), .clk(clock_78_out), .Q(v171));  // open: clr
  Clock clock_78 (.out(clock_78_out));
  Register #(.width(64)) register_79 (.D(value), .en(u179), .clk(clock_79_out), .Q(v179));  // open: clr
  Clock clock_79 (.out(clock_79_out));
  Register #(.width(64)) register_80 (.D(value), .en(u187), .clk(clock_80_out), .Q(v187));  // open: clr
  Clock clock_80 (.out(clock_80_out));
  Register #(.width(64)) register_81 (.D(value), .en(u195), .clk(clock_81_out), .Q(v195));  // open: clr
  Clock clock_81 (.out(clock_81_out));
  Register #(.width(64)) register_82 (.D(value), .en(u203), .clk(clock_82_out), .Q(v203));  // open: clr
  Clock clock_82 (.out(clock_82_out));
  Register #(.width(64)) register_83 (.D(value), .en(u211), .clk(clock_83_out), .Q(v211));  // open: clr
  Clock clock_83 (.out(clock_83_out));
  Register #(.width(64)) register_84 (.D(value), .en(u219), .clk(clock_84_out), .Q(v219));  // open: clr
  Clock clock_84 (.out(clock_84_out));
  Register #(.width(64)) register_85 (.D(value), .en(u4), .clk(clock_85_out), .Q(v4));  // open: clr
  Clock clock_85 (.out(clock_85_out));
  Register #(.width(64)) register_86 (.D(value), .en(u12), .clk(clock_86_out), .Q(v12));  // open: clr
  Clock clock_86 (.out(clock_86_out));
  Register #(.width(64)) register_87 (.D(value), .en(u20), .clk(clock_87_out), .Q(v20));  // open: clr
  Clock clock_87 (.out(clock_87_out));
  Register #(.width(64)) register_88 (.D(value), .en(u28), .clk(clock_88_out), .Q(v28));  // open: clr
  Clock clock_88 (.out(clock_88_out));
  Register #(.width(64)) register_89 (.D(value), .en(u36), .clk(clock_89_out), .Q(v36));  // open: clr
  Clock clock_89 (.out(clock_89_out));
  Register #(.width(64)) register_90 (.D(value), .en(u44), .clk(clock_90_out), .Q(v44));  // open: clr
  Clock clock_90 (.out(clock_90_out));
  Register #(.width(64)) register_91 (.D(value), .en(u52), .clk(clock_91_out), .Q(v52));  // open: clr
  Clock clock_91 (.out(clock_91_out));
  Register #(.width(64)) register_92 (.D(value), .en(u60), .clk(clock_92_out), .Q(v60));  // open: clr
  Clock clock_92 (.out(clock_92_out));
  Register #(.width(64)) register_93 (.D(value), .en(u68), .clk(clock_93_out), .Q(v68));  // open: clr
  Clock clock_93 (.out(clock_93_out));
  Register #(.width(64)) register_94 (.D(value), .en(u76), .clk(clock_94_out), .Q(v76));  // open: clr
  Clock clock_94 (.out(clock_94_out));
  Register #(.width(64)) register_95 (.D(value), .en(u84), .clk(clock_95_out), .Q(v84));  // open: clr
  Clock clock_95 (.out(clock_95_out));
  Register #(.width(64)) register_96 (.D(value), .en(u92), .clk(clock_96_out), .Q(v92));  // open: clr
  Clock clock_96 (.out(clock_96_out));
  Register #(.width(64)) register_97 (.D(value), .en(u100), .clk(clock_97_out), .Q(v100));  // open: clr
  Clock clock_97 (.out(clock_97_out));
  Register #(.width(64)) register_98 (.D(value), .en(u108), .clk(clock_98_out), .Q(v108));  // open: clr
  Clock clock_98 (.out(clock_98_out));
  Register #(.width(64)) register_99 (.D(value), .en(u116), .clk(clock_99_out), .Q(v116));  // open: clr
  Clock clock_99 (.out(clock_99_out));
  Register #(.width(64)) register_100 (.D(value), .en(u124), .clk(clock_100_out), .Q(v124));  // open: clr
  Clock clock_100 (.out(clock_100_out));
  Register #(.width(64)) register_101 (.D(value), .en(u132), .clk(clock_101_out), .Q(v132));  // open: clr
  Clock clock_101 (.out(clock_101_out));
  Register #(.width(64)) register_102 (.D(value), .en(u140), .clk(clock_102_out), .Q(v140));  // open: clr
  Clock clock_102 (.out(clock_102_out));
  Register #(.width(64)) register_103 (.D(value), .en(u148), .clk(clock_103_out), .Q(v148));  // open: clr
  Clock clock_103 (.out(clock_103_out));
  Register #(.width(64)) register_104 (.D(value), .en(u156), .clk(clock_104_out), .Q(v156));  // open: clr
  Clock clock_104 (.out(clock_104_out));
  Register #(.width(64)) register_105 (.D(value), .en(u164), .clk(clock_105_out), .Q(v164));  // open: clr
  Clock clock_105 (.out(clock_105_out));
  Register #(.width(64)) register_106 (.D(value), .en(u172), .clk(clock_106_out), .Q(v172));  // open: clr
  Clock clock_106 (.out(clock_106_out));
  Register #(.width(64)) register_107 (.D(value), .en(u180), .clk(clock_107_out), .Q(v180));  // open: clr
  Clock clock_107 (.out(clock_107_out));
  Register #(.width(64)) register_108 (.D(value), .en(u188), .clk(clock_108_out), .Q(v188));  // open: clr
  Clock clock_108 (.out(clock_108_out));
  Register #(.width(64)) register_109 (.D(value), .en(u196), .clk(clock_109_out), .Q(v196));  // open: clr
  Clock clock_109 (.out(clock_109_out));
  Register #(.width(64)) register_110 (.D(value), .en(u204), .clk(clock_110_out), .Q(v204));  // open: clr
  Clock clock_110 (.out(clock_110_out));
  Register #(.width(64)) register_111 (.D(value), .en(u212), .clk(clock_111_out), .Q(v212));  // open: clr
  Clock clock_111 (.out(clock_111_out));
  Register #(.width(64)) register_112 (.D(value), .en(u220), .clk(clock_112_out), .Q(v220));  // open: clr
  Clock clock_112 (.out(clock_112_out));
  Register #(.width(64)) register_113 (.D(value), .en(u5), .clk(clock_113_out), .Q(v5));  // open: clr
  Clock clock_113 (.out(clock_113_out));
  Register #(.width(64)) register_114 (.D(value), .en(u13), .clk(clock_114_out), .Q(v13));  // open: clr
  Clock clock_114 (.out(clock_114_out));
  Register #(.width(64)) register_115 (.D(value), .en(u21), .clk(clock_115_out), .Q(v21));  // open: clr
  Clock clock_115 (.out(clock_115_out));
  Register #(.width(64)) register_116 (.D(value), .en(u29), .clk(clock_116_out), .Q(v29));  // open: clr
  Clock clock_116 (.out(clock_116_out));
  Register #(.width(64)) register_117 (.D(value), .en(u37), .clk(clock_117_out), .Q(v37));  // open: clr
  Clock clock_117 (.out(clock_117_out));
  Register #(.width(64)) register_118 (.D(value), .en(u45), .clk(clock_118_out), .Q(v45));  // open: clr
  Clock clock_118 (.out(clock_118_out));
  Register #(.width(64)) register_119 (.D(value), .en(u53), .clk(clock_119_out), .Q(v53));  // open: clr
  Clock clock_119 (.out(clock_119_out));
  Register #(.width(64)) register_120 (.D(value), .en(u61), .clk(clock_120_out), .Q(v61));  // open: clr
  Clock clock_120 (.out(clock_120_out));
  Register #(.width(64)) register_121 (.D(value), .en(u69), .clk(clock_121_out), .Q(v69));  // open: clr
  Clock clock_121 (.out(clock_121_out));
  Register #(.width(64)) register_122 (.D(value), .en(u77), .clk(clock_122_out), .Q(v77));  // open: clr
  Clock clock_122 (.out(clock_122_out));
  Register #(.width(64)) register_123 (.D(value), .en(u85), .clk(clock_123_out), .Q(v85));  // open: clr
  Clock clock_123 (.out(clock_123_out));
  Register #(.width(64)) register_124 (.D(value), .en(u93), .clk(clock_124_out), .Q(v93));  // open: clr
  Clock clock_124 (.out(clock_124_out));
  Register #(.width(64)) register_125 (.D(value), .en(u101), .clk(clock_125_out), .Q(v101));  // open: clr
  Clock clock_125 (.out(clock_125_out));
  Register #(.width(64)) register_126 (.D(value), .en(u109), .clk(clock_126_out), .Q(v109));  // open: clr
  Clock clock_126 (.out(clock_126_out));
  Register #(.width(64)) register_127 (.D(value), .en(u117), .clk(clock_127_out), .Q(v117));  // open: clr
  Clock clock_127 (.out(clock_127_out));
  Register #(.width(64)) register_128 (.D(value), .en(u125), .clk(clock_128_out), .Q(v125));  // open: clr
  Clock clock_128 (.out(clock_128_out));
  Register #(.width(64)) register_129 (.D(value), .en(u133), .clk(clock_129_out), .Q(v133));  // open: clr
  Clock clock_129 (.out(clock_129_out));
  Register #(.width(64)) register_130 (.D(value), .en(u141), .clk(clock_130_out), .Q(v141));  // open: clr
  Clock clock_130 (.out(clock_130_out));
  Register #(.width(64)) register_131 (.D(value), .en(u149), .clk(clock_131_out), .Q(v149));  // open: clr
  Clock clock_131 (.out(clock_131_out));
  Register #(.width(64)) register_132 (.D(value), .en(u157), .clk(clock_132_out), .Q(v157));  // open: clr
  Clock clock_132 (.out(clock_132_out));
  Register #(.width(64)) register_133 (.D(value), .en(u165), .clk(clock_133_out), .Q(v165));  // open: clr
  Clock clock_133 (.out(clock_133_out));
  Register #(.width(64)) register_134 (.D(value), .en(u173), .clk(clock_134_out), .Q(v173));  // open: clr
  Clock clock_134 (.out(clock_134_out));
  Register #(.width(64)) register_135 (.D(value), .en(u181), .clk(clock_135_out), .Q(v181));  // open: clr
  Clock clock_135 (.out(clock_135_out));
  Register #(.width(64)) register_136 (.D(value), .en(u189), .clk(clock_136_out), .Q(v189));  // open: clr
  Clock clock_136 (.out(clock_136_out));
  Register #(.width(64)) register_137 (.D(value), .en(u197), .clk(clock_137_out), .Q(v197));  // open: clr
  Clock clock_137 (.out(clock_137_out));
  Register #(.width(64)) register_138 (.D(value), .en(u205), .clk(clock_138_out), .Q(v205));  // open: clr
  Clock clock_138 (.out(clock_138_out));
  Register #(.width(64)) register_139 (.D(value), .en(u213), .clk(clock_139_out), .Q(v213));  // open: clr
  Clock clock_139 (.out(clock_139_out));
  Register #(.width(64)) register_140 (.D(value), .en(u6), .clk(clock_140_out), .Q(v6));  // open: clr
  Clock clock_140 (.out(clock_140_out));
  Register #(.width(64)) register_141 (.D(value), .en(u14), .clk(clock_141_out), .Q(v14));  // open: clr
  Clock clock_141 (.out(clock_141_out));
  Register #(.width(64)) register_142 (.D(value), .en(u22), .clk(clock_142_out), .Q(v22));  // open: clr
  Clock clock_142 (.out(clock_142_out));
  Register #(.width(64)) register_143 (.D(value), .en(u30), .clk(clock_143_out), .Q(v30));  // open: clr
  Clock clock_143 (.out(clock_143_out));
  Register #(.width(64)) register_144 (.D(value), .en(u38), .clk(clock_144_out), .Q(v38));  // open: clr
  Clock clock_144 (.out(clock_144_out));
  Register #(.width(64)) register_145 (.D(value), .en(u46), .clk(clock_145_out), .Q(v46));  // open: clr
  Clock clock_145 (.out(clock_145_out));
  Register #(.width(64)) register_146 (.D(value), .en(u54), .clk(clock_146_out), .Q(v54));  // open: clr
  Clock clock_146 (.out(clock_146_out));
  Register #(.width(64)) register_147 (.D(value), .en(u62), .clk(clock_147_out), .Q(v62));  // open: clr
  Clock clock_147 (.out(clock_147_out));
  Register #(.width(64)) register_148 (.D(value), .en(u70), .clk(clock_148_out), .Q(v70));  // open: clr
  Clock clock_148 (.out(clock_148_out));
  Register #(.width(64)) register_149 (.D(value), .en(u78), .clk(clock_149_out), .Q(v78));  // open: clr
  Clock clock_149 (.out(clock_149_out));
  Register #(.width(64)) register_150 (.D(value), .en(u86), .clk(clock_150_out), .Q(v86));  // open: clr
  Clock clock_150 (.out(clock_150_out));
  Register #(.width(64)) register_151 (.D(value), .en(u94), .clk(clock_151_out), .Q(v94));  // open: clr
  Clock clock_151 (.out(clock_151_out));
  Register #(.width(64)) register_152 (.D(value), .en(u102), .clk(clock_152_out), .Q(v102));  // open: clr
  Clock clock_152 (.out(clock_152_out));
  Register #(.width(64)) register_153 (.D(value), .en(u110), .clk(clock_153_out), .Q(v110));  // open: clr
  Clock clock_153 (.out(clock_153_out));
  Register #(.width(64)) register_154 (.D(value), .en(u118), .clk(clock_154_out), .Q(v118));  // open: clr
  Clock clock_154 (.out(clock_154_out));
  Register #(.width(64)) register_155 (.D(value), .en(u126), .clk(clock_155_out), .Q(v126));  // open: clr
  Clock clock_155 (.out(clock_155_out));
  Register #(.width(64)) register_156 (.D(value), .en(u134), .clk(clock_156_out), .Q(v134));  // open: clr
  Clock clock_156 (.out(clock_156_out));
  Register #(.width(64)) register_157 (.D(value), .en(u142), .clk(clock_157_out), .Q(v142));  // open: clr
  Clock clock_157 (.out(clock_157_out));
  Register #(.width(64)) register_158 (.D(value), .en(u150), .clk(clock_158_out), .Q(v150));  // open: clr
  Clock clock_158 (.out(clock_158_out));
  Register #(.width(64)) register_159 (.D(value), .en(u158), .clk(clock_159_out), .Q(v158));  // open: clr
  Clock clock_159 (.out(clock_159_out));
  Register #(.width(64)) register_160 (.D(value), .en(u166), .clk(clock_160_out), .Q(v166));  // open: clr
  Clock clock_160 (.out(clock_160_out));
  Register #(.width(64)) register_161 (.D(value), .en(u174), .clk(clock_161_out), .Q(v174));  // open: clr
  Clock clock_161 (.out(clock_161_out));
  Register #(.width(64)) register_162 (.D(value), .en(u182), .clk(clock_162_out), .Q(v182));  // open: clr
  Clock clock_162 (.out(clock_162_out));
  Register #(.width(64)) register_163 (.D(value), .en(u190), .clk(clock_163_out), .Q(v190));  // open: clr
  Clock clock_163 (.out(clock_163_out));
  Register #(.width(64)) register_164 (.D(value), .en(u198), .clk(clock_164_out), .Q(v198));  // open: clr
  Clock clock_164 (.out(clock_164_out));
  Register #(.width(64)) register_165 (.D(value), .en(u206), .clk(clock_165_out), .Q(v206));  // open: clr
  Clock clock_165 (.out(clock_165_out));
  Register #(.width(64)) register_166 (.D(value), .en(u214), .clk(clock_166_out), .Q(v214));  // open: clr
  Clock clock_166 (.out(clock_166_out));
  Register #(.width(64)) register_167 (.D(value), .en(u7), .clk(clock_167_out), .Q(v7));  // open: clr
  Clock clock_167 (.out(clock_167_out));
  Register #(.width(64)) register_168 (.D(value), .en(u15), .clk(clock_168_out), .Q(v15));  // open: clr
  Clock clock_168 (.out(clock_168_out));
  Register #(.width(64)) register_169 (.D(value), .en(u23), .clk(clock_169_out), .Q(v23));  // open: clr
  Clock clock_169 (.out(clock_169_out));
  Register #(.width(64)) register_170 (.D(value), .en(u31), .clk(clock_170_out), .Q(v31));  // open: clr
  Clock clock_170 (.out(clock_170_out));
  Register #(.width(64)) register_171 (.D(value), .en(u39), .clk(clock_171_out), .Q(v39));  // open: clr
  Clock clock_171 (.out(clock_171_out));
  Register #(.width(64)) register_172 (.D(value), .en(u47), .clk(clock_172_out), .Q(v47));  // open: clr
  Clock clock_172 (.out(clock_172_out));
  Register #(.width(64)) register_173 (.D(value), .en(u55), .clk(clock_173_out), .Q(v55));  // open: clr
  Clock clock_173 (.out(clock_173_out));
  Register #(.width(64)) register_174 (.D(value), .en(u63), .clk(clock_174_out), .Q(v63));  // open: clr
  Clock clock_174 (.out(clock_174_out));
  Register #(.width(64)) register_175 (.D(value), .en(u71), .clk(clock_175_out), .Q(v71));  // open: clr
  Clock clock_175 (.out(clock_175_out));
  Register #(.width(64)) register_176 (.D(value), .en(u79), .clk(clock_176_out), .Q(v79));  // open: clr
  Clock clock_176 (.out(clock_176_out));
  Register #(.width(64)) register_177 (.D(value), .en(u87), .clk(clock_177_out), .Q(v87));  // open: clr
  Clock clock_177 (.out(clock_177_out));
  Register #(.width(64)) register_178 (.D(value), .en(u95), .clk(clock_178_out), .Q(v95));  // open: clr
  Clock clock_178 (.out(clock_178_out));
  Register #(.width(64)) register_179 (.D(value), .en(u103), .clk(clock_179_out), .Q(v103));  // open: clr
  Clock clock_179 (.out(clock_179_out));
  Register #(.width(64)) register_180 (.D(value), .en(u111), .clk(clock_180_out), .Q(v111));  // open: clr
  Clock clock_180 (.out(clock_180_out));
  Register #(.width(64)) register_181 (.D(value), .en(u119), .clk(clock_181_out), .Q(v119));  // open: clr
  Clock clock_181 (.out(clock_181_out));
  Register #(.width(64)) register_182 (.D(value), .en(u127), .clk(clock_182_out), .Q(v127));  // open: clr
  Clock clock_182 (.out(clock_182_out));
  Register #(.width(64)) register_183 (.D(value), .en(u135), .clk(clock_183_out), .Q(v135));  // open: clr
  Clock clock_183 (.out(clock_183_out));
  Register #(.width(64)) register_184 (.D(value), .en(u143), .clk(clock_184_out), .Q(v143));  // open: clr
  Clock clock_184 (.out(clock_184_out));
  Register #(.width(64)) register_185 (.D(value), .en(u151), .clk(clock_185_out), .Q(v151));  // open: clr
  Clock clock_185 (.out(clock_185_out));
  Register #(.width(64)) register_186 (.D(value), .en(u159), .clk(clock_186_out), .Q(v159));  // open: clr
  Clock clock_186 (.out(clock_186_out));
  Register #(.width(64)) register_187 (.D(value), .en(u167), .clk(clock_187_out), .Q(v167));  // open: clr
  Clock clock_187 (.out(clock_187_out));
  Register #(.width(64)) register_188 (.D(value), .en(u175), .clk(clock_188_out), .Q(v175));  // open: clr
  Clock clock_188 (.out(clock_188_out));
  Register #(.width(64)) register_189 (.D(value), .en(u183), .clk(clock_189_out), .Q(v183));  // open: clr
  Clock clock_189 (.out(clock_189_out));
  Register #(.width(64)) register_190 (.D(value), .en(u191), .clk(clock_190_out), .Q(v191));  // open: clr
  Clock clock_190 (.out(clock_190_out));
  Register #(.width(64)) register_191 (.D(value), .en(u199), .clk(clock_191_out), .Q(v199));  // open: clr
  Clock clock_191 (.out(clock_191_out));
  Register #(.width(64)) register_192 (.D(value), .en(u207), .clk(clock_192_out), .Q(v207));  // open: clr
  Clock clock_192 (.out(clock_192_out));
  Register #(.width(64)) register_193 (.D(value), .en(u215), .clk(clock_193_out), .Q(v215));  // open: clr
  Clock clock_193 (.out(clock_193_out));
  Register #(.width(64)) register_194 (.D(value), .en(u8), .clk(clock_194_out), .Q(v8));  // open: clr
  Clock clock_194 (.out(clock_194_out));
  Register #(.width(64)) register_195 (.D(value), .en(u16), .clk(clock_195_out), .Q(v16));  // open: clr
  Clock clock_195 (.out(clock_195_out));
  Register #(.width(64)) register_196 (.D(value), .en(u24), .clk(clock_196_out), .Q(v24));  // open: clr
  Clock clock_196 (.out(clock_196_out));
  Register #(.width(64)) register_197 (.D(value), .en(u32), .clk(clock_197_out), .Q(v32));  // open: clr
  Clock clock_197 (.out(clock_197_out));
  Register #(.width(64)) register_198 (.D(value), .en(u40), .clk(clock_198_out), .Q(v40));  // open: clr
  Clock clock_198 (.out(clock_198_out));
  Register #(.width(64)) register_199 (.D(value), .en(u48), .clk(clock_199_out), .Q(v48));  // open: clr
  Clock clock_199 (.out(clock_199_out));
  Register #(.width(64)) register_200 (.D(value), .en(u56), .clk(clock_200_out), .Q(v56));  // open: clr
  Clock clock_200 (.out(clock_200_out));
  Register #(.width(64)) register_201 (.D(value), .en(u64), .clk(clock_201_out), .Q(v64));  // open: clr
  Clock clock_201 (.out(clock_201_out));
  Register #(.width(64)) register_202 (.D(value), .en(u72), .clk(clock_202_out), .Q(v72));  // open: clr
  Clock clock_202 (.out(clock_202_out));
  Register #(.width(64)) register_203 (.D(value), .en(u80), .clk(clock_203_out), .Q(v80));  // open: clr
  Clock clock_203 (.out(clock_203_out));
  Register #(.width(64)) register_204 (.D(value), .en(u88), .clk(clock_204_out), .Q(v88));  // open: clr
  Clock clock_204 (.out(clock_204_out));
  Register #(.width(64)) register_205 (.D(value), .en(u96), .clk(clock_205_out), .Q(v96));  // open: clr
  Clock clock_205 (.out(clock_205_out));
  Register #(.width(64)) register_206 (.D(value), .en(u104), .clk(clock_206_out), .Q(v104));  // open: clr
  Clock clock_206 (.out(clock_206_out));
  Register #(.width(64)) register_207 (.D(value), .en(u112), .clk(clock_207_out), .Q(v112));  // open: clr
  Clock clock_207 (.out(clock_207_out));
  Register #(.width(64)) register_208 (.D(value), .en(u120), .clk(clock_208_out), .Q(v120));  // open: clr
  Clock clock_208 (.out(clock_208_out));
  Register #(.width(64)) register_209 (.D(value), .en(u128), .clk(clock_209_out), .Q(v128));  // open: clr
  Clock clock_209 (.out(clock_209_out));
  Register #(.width(64)) register_210 (.D(value), .en(u136), .clk(clock_210_out), .Q(v136));  // open: clr
  Clock clock_210 (.out(clock_210_out));
  Register #(.width(64)) register_211 (.D(value), .en(u144), .clk(clock_211_out), .Q(v144));  // open: clr
  Clock clock_211 (.out(clock_211_out));
  Register #(.width(64)) register_212 (.D(value), .en(u152), .clk(clock_212_out), .Q(v152));  // open: clr
  Clock clock_212 (.out(clock_212_out));
  Register #(.width(64)) register_213 (.D(value), .en(u160), .clk(clock_213_out), .Q(v160));  // open: clr
  Clock clock_213 (.out(clock_213_out));
  Register #(.width(64)) register_214 (.D(value), .en(u168), .clk(clock_214_out), .Q(v168));  // open: clr
  Clock clock_214 (.out(clock_214_out));
  Register #(.width(64)) register_215 (.D(value), .en(u176), .clk(clock_215_out), .Q(v176));  // open: clr
  Clock clock_215 (.out(clock_215_out));
  Register #(.width(64)) register_216 (.D(value), .en(u184), .clk(clock_216_out), .Q(v184));  // open: clr
  Clock clock_216 (.out(clock_216_out));
  Register #(.width(64)) register_217 (.D(value), .en(u192), .clk(clock_217_out), .Q(v192));  // open: clr
  Clock clock_217 (.out(clock_217_out));
  Register #(.width(64)) register_218 (.D(value), .en(u200), .clk(clock_218_out), .Q(v200));  // open: clr
  Clock clock_218 (.out(clock_218_out));
  Register #(.width(64)) register_219 (.D(value), .en(u208), .clk(clock_219_out), .Q(v208));  // open: clr
  Clock clock_219 (.out(clock_219_out));
  Register #(.width(64)) register_220 (.D(value), .en(u216), .clk(clock_220_out), .Q(v216));  // open: clr
  Clock clock_220 (.out(clock_220_out));
  Register #(.width(64)) register_221 (.D(value), .en(u221), .clk(clock_221_out), .Q(corein0));  // open: clr
  Clock clock_221 (.out(clock_221_out));
  Register #(.width(64)) register_222 (.D(value), .en(u225), .clk(clock_222_out), .Q(output1r));  // open: clr
  Clock clock_222 (.out(clock_222_out));
  Register #(.width(64)) register_223 (.D(value), .en(u229), .clk(clock_223_out), .Q(output5r));  // open: clr
  Clock clock_223 (.out(clock_223_out));
  Register #(.width(64)) register_224 (.D(value), .en(u233), .clk(clock_224_out), .Q(output9r));  // open: clr
  Clock clock_224 (.out(clock_224_out));
  Register #(.width(64)) register_225 (.D(value), .en(u237), .clk(clock_225_out), .Q(output13r));  // open: clr
  Clock clock_225 (.out(clock_225_out));
  Register #(.width(64)) register_226 (.D(value), .en(u241), .clk(clock_226_out), .Q(output1d));  // open: clr
  Clock clock_226 (.out(clock_226_out));
  Register #(.width(64)) register_227 (.D(value), .en(u245), .clk(clock_227_out), .Q(output5d));  // open: clr
  Clock clock_227 (.out(clock_227_out));
  Register #(.width(64)) register_228 (.D(value), .en(u249), .clk(clock_228_out), .Q(output9d));  // open: clr
  Clock clock_228 (.out(clock_228_out));
  Register #(.width(64)) register_229 (.D(value), .en(u253), .clk(clock_229_out), .Q(output13d));  // open: clr
  Clock clock_229 (.out(clock_229_out));
  Register #(.width(64)) register_230 (.D(value), .en(u222), .clk(clock_230_out), .Q(clockout0));  // open: clr
  Clock clock_230 (.out(clock_230_out));
  Register #(.width(64)) register_231 (.D(value), .en(u226), .clk(clock_231_out), .Q(output2r));  // open: clr
  Clock clock_231 (.out(clock_231_out));
  Register #(.width(64)) register_232 (.D(value), .en(u230), .clk(clock_232_out), .Q(output6r));  // open: clr
  Clock clock_232 (.out(clock_232_out));
  Register #(.width(64)) register_233 (.D(value), .en(u234), .clk(clock_233_out), .Q(output10r));  // open: clr
  Clock clock_233 (.out(clock_233_out));
  Register #(.width(64)) register_234 (.D(value), .en(u238), .clk(clock_234_out), .Q(output14r));  // open: clr
  Clock clock_234 (.out(clock_234_out));
  Register #(.width(64)) register_235 (.D(value), .en(u242), .clk(clock_235_out), .Q(output2d));  // open: clr
  Clock clock_235 (.out(clock_235_out));
  Register #(.width(64)) register_236 (.D(value), .en(u246), .clk(clock_236_out), .Q(output6d));  // open: clr
  Clock clock_236 (.out(clock_236_out));
  Register #(.width(64)) register_237 (.D(value), .en(u250), .clk(clock_237_out), .Q(output10d));  // open: clr
  Clock clock_237 (.out(clock_237_out));
  Register #(.width(64)) register_238 (.D(value), .en(u254), .clk(clock_238_out), .Q(output14d));  // open: clr
  Clock clock_238 (.out(clock_238_out));
  Register #(.width(64)) register_239 (.D(value), .en(u223), .clk(clock_239_out), .Q(freqout0));  // open: clr
  Clock clock_239 (.out(clock_239_out));
  Register #(.width(64)) register_240 (.D(value), .en(u227), .clk(clock_240_out), .Q(output3r));  // open: clr
  Clock clock_240 (.out(clock_240_out));
  Register #(.width(64)) register_241 (.D(value), .en(u231), .clk(clock_241_out), .Q(output7r));  // open: clr
  Clock clock_241 (.out(clock_241_out));
  Register #(.width(64)) register_242 (.D(value), .en(u235), .clk(clock_242_out), .Q(output11r));  // open: clr
  Clock clock_242 (.out(clock_242_out));
  Register #(.width(64)) register_243 (.D(value), .en(u239), .clk(clock_243_out), .Q(output15r));  // open: clr
  Clock clock_243 (.out(clock_243_out));
  Register #(.width(64)) register_244 (.D(value), .en(u243), .clk(clock_244_out), .Q(output3d));  // open: clr
  Clock clock_244 (.out(clock_244_out));
  Register #(.width(64)) register_245 (.D(value), .en(u247), .clk(clock_245_out), .Q(output7d));  // open: clr
  Clock clock_245 (.out(clock_245_out));
  Register #(.width(64)) register_246 (.D(value), .en(u251), .clk(clock_246_out), .Q(output11d));  // open: clr
  Clock clock_246 (.out(clock_246_out));
  Register #(.width(64)) register_247 (.D(value), .en(u255), .clk(clock_247_out), .Q(output15d));  // open: clr
  Clock clock_247 (.out(clock_247_out));
  Register #(.width(64)) register_248 (.D(value), .en(u224), .clk(clock_248_out), .Q(output0));  // open: clr
  Clock clock_248 (.out(clock_248_out));
  Register #(.width(64)) register_249 (.D(value), .en(u228), .clk(clock_249_out), .Q(output4r));  // open: clr
  Clock clock_249 (.out(clock_249_out));
  Register #(.width(64)) register_250 (.D(value), .en(u232), .clk(clock_250_out), .Q(output8r));  // open: clr
  Clock clock_250 (.out(clock_250_out));
  Register #(.width(64)) register_251 (.D(value), .en(u236), .clk(clock_251_out), .Q(output12r));  // open: clr
  Clock clock_251 (.out(clock_251_out));
  Register #(.width(64)) register_252 (.D(value), .en(u240), .clk(clock_252_out), .Q(output16r));  // open: clr
  Clock clock_252 (.out(clock_252_out));
  Register #(.width(64)) register_253 (.D(value), .en(u244), .clk(clock_253_out), .Q(output4d));  // open: clr
  Clock clock_253 (.out(clock_253_out));
  Register #(.width(64)) register_254 (.D(value), .en(u248), .clk(clock_254_out), .Q(output8d));  // open: clr
  Clock clock_254 (.out(clock_254_out));
  Register #(.width(64)) register_255 (.D(value), .en(u252), .clk(clock_255_out), .Q(output12d));  // open: clr
  Clock clock_255 (.out(clock_255_out));
  Register #(.width(64)) register_256 (.D(value), .en(u256), .clk(clock_256_out), .Q(output16d));  // open: clr
  Clock clock_256 (.out(clock_256_out));
  Multiplexer #(.select(8), .width(64)) multiplexer_1 (
    .in0(v1), .in1(v2), .in2(v3), .in3(v4), .in4(v5), .in5(v6), .in6(v7), .in7(v8), .in8(v9), .in9(v10),
    .in10(v11), .in11(v12), .in12(v13), .in13(v14), .in14(v15), .in15(v16), .in16(v17), .in17(v18),
    .in18(v19), .in19(v20), .in20(v21), .in21(v22), .in22(v23), .in23(v24), .in24(v25), .in25(v26),
    .in26(v27), .in27(v28), .in28(v29), .in29(v30), .in30(v31), .in31(v32), .in32(v33), .in33(v34),
    .in34(v35), .in35(v36), .in36(v37), .in37(v38), .in38(v39), .in39(v40), .in40(v41), .in41(v42),
    .in42(v43), .in43(v44), .in44(v45), .in45(v46), .in46(v47), .in47(v48), .in48(v49), .in49(v50),
    .in50(v51), .in51(v52), .in52(v53), .in53(v54), .in54(v55), .in55(v56), .in56(v57), .in57(v58),
    .in58(v59), .in59(v60), .in60(v61), .in61(v62), .in62(v63), .in63(v64), .in64(v65), .in65(v66),
    .in66(v67), .in67(v68), .in68(v69), .in69(v70), .in70(v71), .in71(v72), .in72(v73), .in73(v74),
    .in74(v75), .in75(v76), .in76(v77), .in77(v78), .in78(v79), .in79(v80), .in80(v81), .in81(v82),
    .in82(v83), .in83(v84), .in84(v85), .in85(v86), .in86(v87), .in87(v88), .in88(v89), .in89(v90),
    .in90(v91), .in91(v92), .in92(v93), .in93(v94), .in94(v95), .in95(v96), .in96(v97), .in97(v98),
    .in98(v99), .in99(v100), .in100(v101), .in101(v102), .in102(v103), .in103(v104), .in104(v105),
    .in105(v106), .in106(v107), .in107(v108), .in108(v109), .in109(v110), .in110(v111), .in111(v112),
    .in112(v113), .in113(v114), .in114(v115), .in115(v116), .in116(v117), .in117(v118), .in118(v119),
    .in119(v120), .in120(v121), .in121(v122), .in122(v123), .in123(v124), .in124(v125), .in125(v126),
    .in126(v127), .in127(v128), .in128(v129), .in129(v130), .in130(v131), .in131(v132), .in132(v133),
    .in133(v134), .in134(v135), .in135(v136), .in136(v137), .in137(v138), .in138(v139), .in139(v140),
    .in140(v141), .in141(v142), .in142(v143), .in143(v144), .in144(v145), .in145(v146), .in146(v147),
    .in147(v148), .in148(v149), .in149(v150), .in150(v151), .in151(v152), .in152(v153), .in153(v154),
    .in154(v155), .in155(v156), .in156(v157), .in157(v158), .in158(v159), .in159(v160), .in160(v161),
    .in161(v162), .in162(v163), .in163(v164), .in164(v165), .in165(v166), .in166(v167), .in167(v168),
    .in168(v169), .in169(v170), .in170(v171), .in171(v172), .in172(v173), .in173(v174), .in174(v175),
    .in175(v176), .in176(v177), .in177(v178), .in178(v179), .in179(v180), .in180(v181), .in181(v182),
    .in182(v183), .in183(v184), .in184(v185), .in185(v186), .in186(v187), .in187(v188), .in188(v189),
    .in189(v190), .in190(v191), .in191(v192), .in192(v193), .in193(v194), .in194(v195), .in195(v196),
    .in196(v197), .in197(v198), .in198(v199), .in199(v200), .in200(v201), .in201(v202), .in202(v203),
    .in203(v204), .in204(v205), .in205(v206), .in206(v207), .in207(v208), .in208(v209), .in209(v210),
    .in210(v211), .in211(v212), .in212(v213), .in213(v214), .in214(v215), .in215(v216), .in216(v217),
    .in217(v218), .in218(v219), .in219(v220), .in220(coreout0), .in221(clockin0), .in222(freqin0),
    .in223(input0), .in224(input1r), .in225(input2r), .in226(input3r), .in227(input4r), .in228(input5r),
    .in229(input6r), .in230(input7r), .in231(input8r), .in232(input9r), .in233(input10r), .in234(input11r),
    .in235(input12r), .in236(input13r), .in237(input14r), .in238(input15r), .in239(input16r),
    .in240(input1d), .in241(input2d), .in242(input3d), .in243(input4d), .in244(input5d), .in245(input6d),
    .in246(input7d), .in247(input8d), .in248(input9d), .in249(input10d), .in250(input11d), .in251(input12d),
    .in252(input13d), .in253(input14d), .in254(input15d), .in255(input16d), .out(regXout), .sel(regX_t));
  Multiplexer #(.select(8), .width(64)) multiplexer_2 (
    .in0(v1), .in1(v2), .in2(v3), .in3(v4), .in4(v5), .in5(v6), .in6(v7), .in7(v8), .in8(v9), .in9(v10),
    .in10(v11), .in11(v12), .in12(v13), .in13(v14), .in14(v15), .in15(v16), .in16(v17), .in17(v18),
    .in18(v19), .in19(v20), .in20(v21), .in21(v22), .in22(v23), .in23(v24), .in24(v25), .in25(v26),
    .in26(v27), .in27(v28), .in28(v29), .in29(v30), .in30(v31), .in31(v32), .in32(v33), .in33(v34),
    .in34(v35), .in35(v36), .in36(v37), .in37(v38), .in38(v39), .in39(v40), .in40(v41), .in41(v42),
    .in42(v43), .in43(v44), .in44(v45), .in45(v46), .in46(v47), .in47(v48), .in48(v49), .in49(v50),
    .in50(v51), .in51(v52), .in52(v53), .in53(v54), .in54(v55), .in55(v56), .in56(v57), .in57(v58),
    .in58(v59), .in59(v60), .in60(v61), .in61(v62), .in62(v63), .in63(v64), .in64(v65), .in65(v66),
    .in66(v67), .in67(v68), .in68(v69), .in69(v70), .in70(v71), .in71(v72), .in72(v73), .in73(v74),
    .in74(v75), .in75(v76), .in76(v77), .in77(v78), .in78(v79), .in79(v80), .in80(v81), .in81(v82),
    .in82(v83), .in83(v84), .in84(v85), .in85(v86), .in86(v87), .in87(v88), .in88(v89), .in89(v90),
    .in90(v91), .in91(v92), .in92(v93), .in93(v94), .in94(v95), .in95(v96), .in96(v97), .in97(v98),
    .in98(v99), .in99(v100), .in100(v101), .in101(v102), .in102(v103), .in103(v104), .in104(v105),
    .in105(v106), .in106(v107), .in107(v108), .in108(v109), .in109(v110), .in110(v111), .in111(v112),
    .in112(v113), .in113(v114), .in114(v115), .in115(v116), .in116(v117), .in117(v118), .in118(v119),
    .in119(v120), .in120(v121), .in121(v122), .in122(v123), .in123(v124), .in124(v125), .in125(v126),
    .in126(v127), .in127(v128), .in128(v129), .in129(v130), .in130(v131), .in131(v132), .in132(v133),
    .in133(v134), .in134(v135), .in135(v136), .in136(v137), .in137(v138), .in138(v139), .in139(v140),
    .in140(v141), .in141(v142), .in142(v143), .in143(v144), .in144(v145), .in145(v146), .in146(v147),
    .in147(v148), .in148(v149), .in149(v150), .in150(v151), .in151(v152), .in152(v153), .in153(v154),
    .in154(v155), .in155(v156), .in156(v157), .in157(v158), .in158(v159), .in159(v160), .in160(v161),
    .in161(v162), .in162(v163), .in163(v164), .in164(v165), .in165(v166), .in166(v167), .in167(v168),
    .in168(v169), .in169(v170), .in170(v171), .in171(v172), .in172(v173), .in173(v174), .in174(v175),
    .in175(v176), .in176(v177), .in177(v178), .in178(v179), .in179(v180), .in180(v181), .in181(v182),
    .in182(v183), .in183(v184), .in184(v185), .in185(v186), .in186(v187), .in187(v188), .in188(v189),
    .in189(v190), .in190(v191), .in191(v192), .in192(v193), .in193(v194), .in194(v195), .in195(v196),
    .in196(v197), .in197(v198), .in198(v199), .in199(v200), .in200(v201), .in201(v202), .in202(v203),
    .in203(v204), .in204(v205), .in205(v206), .in206(v207), .in207(v208), .in208(v209), .in209(v210),
    .in210(v211), .in211(v212), .in212(v213), .in213(v214), .in214(v215), .in215(v216), .in216(v217),
    .in217(v218), .in218(v219), .in219(v220), .in220(coreout0), .in221(clockin0), .in222(freqin0),
    .in223(input0), .in224(input1r), .in225(input2r), .in226(input3r), .in227(input4r), .in228(input5r),
    .in229(input6r), .in230(input7r), .in231(input8r), .in232(input9r), .in233(input10r), .in234(input11r),
    .in235(input12r), .in236(input13r), .in237(input14r), .in238(input15r), .in239(input16r),
    .in240(input1d), .in241(input2d), .in242(input3d), .in243(input4d), .in244(input5d), .in245(input6d),
    .in246(input7d), .in247(input8d), .in248(input9d), .in249(input10d), .in250(input11d), .in251(input12d),
    .in252(input13d), .in253(input14d), .in254(input15d), .in255(input16d), .out(regYout), .sel(regY_t));
  Multiplexer #(.select(8), .width(64)) multiplexer_3 (
    .in0(v1), .in1(v2), .in2(v3), .in3(v4), .in4(v5), .in5(v6), .in6(v7), .in7(v8), .in8(v9), .in9(v10),
    .in10(v11), .in11(v12), .in12(v13), .in13(v14), .in14(v15), .in15(v16), .in16(v17), .in17(v18),
    .in18(v19), .in19(v20), .in20(v21), .in21(v22), .in22(v23), .in23(v24), .in24(v25), .in25(v26),
    .in26(v27), .in27(v28), .in28(v29), .in29(v30), .in30(v31), .in31(v32), .in32(v33), .in33(v34),
    .in34(v35), .in35(v36), .in36(v37), .in37(v38), .in38(v39), .in39(v40), .in40(v41), .in41(v42),
    .in42(v43), .in43(v44), .in44(v45), .in45(v46), .in46(v47), .in47(v48), .in48(v49), .in49(v50),
    .in50(v51), .in51(v52), .in52(v53), .in53(v54), .in54(v55), .in55(v56), .in56(v57), .in57(v58),
    .in58(v59), .in59(v60), .in60(v61), .in61(v62), .in62(v63), .in63(v64), .in64(v65), .in65(v66),
    .in66(v67), .in67(v68), .in68(v69), .in69(v70), .in70(v71), .in71(v72), .in72(v73), .in73(v74),
    .in74(v75), .in75(v76), .in76(v77), .in77(v78), .in78(v79), .in79(v80), .in80(v81), .in81(v82),
    .in82(v83), .in83(v84), .in84(v85), .in85(v86), .in86(v87), .in87(v88), .in88(v89), .in89(v90),
    .in90(v91), .in91(v92), .in92(v93), .in93(v94), .in94(v95), .in95(v96), .in96(v97), .in97(v98),
    .in98(v99), .in99(v100), .in100(v101), .in101(v102), .in102(v103), .in103(v104), .in104(v105),
    .in105(v106), .in106(v107), .in107(v108), .in108(v109), .in109(v110), .in110(v111), .in111(v112),
    .in112(v113), .in113(v114), .in114(v115), .in115(v116), .in116(v117), .in117(v118), .in118(v119),
    .in119(v120), .in120(v121), .in121(v122), .in122(v123), .in123(v124), .in124(v125), .in125(v126),
    .in126(v127), .in127(v128), .in128(v129), .in129(v130), .in130(v131), .in131(v132), .in132(v133),
    .in133(v134), .in134(v135), .in135(v136), .in136(v137), .in137(v138), .in138(v139), .in139(v140),
    .in140(v141), .in141(v142), .in142(v143), .in143(v144), .in144(v145), .in145(v146), .in146(v147),
    .in147(v148), .in148(v149), .in149(v150), .in150(v151), .in151(v152), .in152(v153), .in153(v154),
    .in154(v155), .in155(v156), .in156(v157), .in157(v158), .in158(v159), .in159(v160), .in160(v161),
    .in161(v162), .in162(v163), .in163(v164), .in164(v165), .in165(v166), .in166(v167), .in167(v168),
    .in168(v169), .in169(v170), .in170(v171), .in171(v172), .in172(v173), .in173(v174), .in174(v175),
    .in175(v176), .in176(v177), .in177(v178), .in178(v179), .in179(v180), .in180(v181), .in181(v182),
    .in182(v183), .in183(v184), .in184(v185), .in185(v186), .in186(v187), .in187(v188), .in188(v189),
    .in189(v190), .in190(v191), .in191(v192), .in192(v193), .in193(v194), .in194(v195), .in195(v196),
    .in196(v197), .in197(v198), .in198(v199), .in199(v200), .in200(v201), .in201(v202), .in202(v203),
    .in203(v204), .in204(v205), .in205(v206), .in206(v207), .in207(v208), .in208(v209), .in209(v210),
    .in210(v211), .in211(v212), .in212(v213), .in213(v214), .in214(v215), .in215(v216), .in216(v217),
    .in217(v218), .in218(v219), .in219(v220), .in220(coreout0), .in221(clockin0), .in222(freqin0),
    .in223(input0), .in224(input1r), .in225(input2r), .in226(input3r), .in227(input4r), .in228(input5r),
    .in229(input6r), .in230(input7r), .in231(input8r), .in232(input9r), .in233(input10r), .in234(input11r),
    .in235(input12r), .in236(input13r), .in237(input14r), .in238(input15r), .in239(input16r),
    .in240(input1d), .in241(input2d), .in242(input3d), .in243(input4d), .in244(input5d), .in245(input6d),
    .in246(input7d), .in247(input8d), .in248(input9d), .in249(input10d), .in250(input11d), .in251(input12d),
    .in252(input13d), .in253(input14d), .in254(input15d), .in255(input16d), .out(regZout), .sel(regZ_t));

  // Other names for the same wires on the sheet: v221[63:0] = coreout0; v222[63:0] = clockin0; v223[63:0] = freqin0;
  //   v224[63:0] = input0; v225[63:0] = input1r; v226[63:0] = input2r; v227[63:0] = input3r; v228[63:0] = input4r;
  //   v229[63:0] = input5r; v230[63:0] = input6r; v231[63:0] = input7r; v232[63:0] = input8r; v233[63:0] = input9r;
  //   v234[63:0] = input10r; v235[63:0] = input11r; v236[63:0] = input12r; v237[63:0] = input13r;
  //   v238[63:0] = input14r; v239[63:0] = input15r; v240[63:0] = input16r; v241[63:0] = input1d; v242[63:0] = input2d;
  //   v243[63:0] = input3d; v244[63:0] = input4d; v245[63:0] = input5d; v246[63:0] = input6d; v247[63:0] = input7d;
  //   v248[63:0] = input8d; v249[63:0] = input9d; v250[63:0] = input10d; v251[63:0] = input11d; v252[63:0] = input12d;
  //   v253[63:0] = input13d; v254[63:0] = input14d; v255[63:0] = input15d; v256[63:0] = input16d
endmodule

module core (
  input  [63:0] corein0,
  input  [63:0] clockin0,
  input  [63:0] freqin0,
  input  [63:0] input0,
  input  [63:0] input1r,
  input  [63:0] input2r,
  input  [63:0] input3r,
  input  [63:0] input4r,
  input  [63:0] input5r,
  input  [63:0] input6r,
  input  [63:0] input7r,
  input  [63:0] input8r,
  input  [63:0] input9r,
  input  [63:0] input10r,
  input  [63:0] input11r,
  input  [63:0] input12r,
  input  [63:0] input13r,
  input  [63:0] input14r,
  input  [63:0] input1r5,
  input  [63:0] input16r,
  input  [63:0] input1d,
  input  [63:0] input2d,
  input  [63:0] input3d,
  input  [63:0] input4d,
  input  [63:0] input5d,
  input  [63:0] input6d,
  input  [63:0] input7d,
  input  [63:0] input8d,
  input  [63:0] input9d,
  input  [63:0] input10d,
  input  [63:0] input11d,
  input  [63:0] input12d,
  input  [63:0] input13d,
  input  [63:0] input14d,
  input  [63:0] input15d,
  input  [63:0] input16d,
  output [63:0] coreout0,
  output [63:0] clockout0,
  output [63:0] freqout0,
  output [63:0] output0,
  output [63:0] output1r,
  output [63:0] output2r,
  output [63:0] output3r,
  output [63:0] output4r,
  output [63:0] output5r,
  output [63:0] output6r,
  output [63:0] output7r,
  output [63:0] output8r,
  output [63:0] output9r,
  output [63:0] output10r,
  output [63:0] output11r,
  output [63:0] output12r,
  output [63:0] output13r,
  output [63:0] output14r,
  output [63:0] output15r,
  output [63:0] output16r,
  output [63:0] output1d,
  output [63:0] output2d,
  output [63:0] output3d,
  output [63:0] output4d,
  output [63:0] output5d,
  output [63:0] output6d,
  output [63:0] output7d,
  output [63:0] output8d,
  output [63:0] output9d,
  output [63:0] output10d,
  output [63:0] output11d,
  output [63:0] output12d,
  output [63:0] output13d,
  output [63:0] output14d,
  output [63:0] output15d,
  output [63:0] output16d
);

  wire adder_1_cout, and_2_out, and_3_out, and_4_out, and_5_out, and_6_out, and_10_out, bitselector_9_out,
       bitselector_13_out, bitselector_14_out, clock_1_out, clock_2_out, clock_3_out, clock_4_out,
       clock_5_out, clock_6_out, comparator_1_eq, comparator_2_eq, comparator_3_eq, comparator_4_eq,
       comparator_5_eq, comparator_6_eq, comparator_7_eq, comparator_7_lt, comparator_8_eq, comparator_9_eq,
       comparator_10_eq, comparator_11_eq, comparator_11_gt, comparator_11_lt, comparator_12_eq,
       comparator_12_lt, comparator_13_eq, counter_2_q, demultiplexer_1_out1, demultiplexer_1_out2,
       demultiplexer_1_out3, fpcomparator_1_p3, fpcomparator_1_p4, multiplexer_1_out, multiplexer_5_out,
       multiplexer_10_out, not_2_out, not_6_out, or_1_out, or_3_out, or_7_out, or_8_out, or_9_out,
       register_3_q, rgb_video_1_p1, subtractor_1_bout;
  wire [1:0] bitselector_15_out, bitselector_18_out;
  wire [3:0] bitselector_6_out, bitselector_7_out;
  wire [5:0] bitselector_8_out, bitselector_10_out, bitselector_11_out, bitselector_12_out;
  wire [7:0] bitselector_5_out, bitselector_20_out, rgb_video_1_p3, rgb_video_1_p4;
  wire [15:0] bitselector_1_out, bitselector_2_out, bitselector_3_out, bitselector_4_out;
  wire [23:0] bitselector_19_out, rgb_video_1_p5;
  wire [25:0] bitselector_16_out, bitselector_17_out, counter_3_q, multiplexer_8_out, multiplexer_9_out;
  wire [31:0] counter_1_q;
  wire [63:0] adder_1_out, and_1_out, and_7_out, and_8_out, and_9_out, bit_extender_1_out,
       bit_extender_2_out, buffer_1_out, divider_1_out, divider_1_rem, fpadder_1_out, fpdivider_1_out,
       fpmultiplier_1_out, fpnegator_1_p2, fpsubtractor_1_out, fptoint_1_p1, fptoint_2_p1, fptoint_3_p1,
       fptoint_4_p1, inttofp_1_p1, multiplexer_2_out, multiplexer_3_out, multiplexer_4_out,
       multiplexer_6_out, multiplexer_7_out, multiplexer_11_out, multiplexer_12_out, multiplier_1_cout,
       multiplier_1_out, nand_1_out, negator_1_out, nor_1_out, not_1_out, not_3_out, not_4_out, not_5_out,
       or_2_out, or_4_out, or_5_out, or_6_out, ram_1_dout, ram_2_dout, ram_3_dout, ram_4_dout, register_1_q,
       register_2_q, registry_1_regxout, registry_1_regyout, registry_1_regzout, shifter_1_out,
       shifter_2_out, shifter_3_out, shifter_4_out, shifter_5_out, shifter_6_out, shifter_7_out,
       shifter_8_out, subtractor_1_out, xnor_1_out, xor_1_out;

  BitSelector #(.group(16), .width(64)) bitselector_1 (.in(register_1_q), .out(bitselector_1_out), .sel(2'b11));
  BitSelector #(.group(16), .width(64)) bitselector_2 (.in(register_1_q), .out(bitselector_2_out), .sel(2'b10));
  BitSelector #(.group(16), .width(64)) bitselector_3 (.in(register_1_q), .out(bitselector_3_out), .sel(2'b01));
  BitSelector #(.group(16), .width(64)) bitselector_4 (.in(register_1_q), .out(bitselector_4_out), .sel(2'b00));
  Register #(.trigger("falling"), .width(64)) register_1 (
    .D(multiplexer_12_out), .en(or_1_out), .clk(clock_1_out), .Q(register_1_q));  // open: clr
  or or_1 (or_1_out, or_8_out, comparator_1_eq);
  Comparator #(.width(64)) comparator_1 (.a({64{1'b0}}), .b(register_1_q), .eq(comparator_1_eq));  // open: gt, lt
  Clock clock_1 (.out(clock_1_out));
  registry registry_1 (
    .value(multiplexer_7_out), .update(or_7_out), .regX(bitselector_1_out), .regY(bitselector_2_out),
    .regZ(bitselector_3_out), .coreout0(corein0), .clockin0(clockin0), .freqin0(freqin0), .input0(input0),
    .input1r(input1r), .input2r(input2r), .input3r(input3r), .input4r(input4r), .input5r(input5r),
    .input6r(input6r), .input7r(input7r), .input8r(input8r), .input9r(input9r), .input10r(input10r),
    .input11r(input11r), .input12r(input12r), .input13r(input13r), .input14r(input14r), .input15r(input1r5),
    .input16r(input16r), .input1d(input1d), .input2d(input2d), .input3d(input3d), .input4d(input4d),
    .input5d(input5d), .input6d(input6d), .input7d(input7d), .input8d(input8d), .input9d(input9d),
    .input10d(input10d), .input11d(input11d), .input12d(input12d), .input13d(input13d), .input14d(input14d),
    .input15d(input15d), .input16d(input16d), .regXout(registry_1_regxout), .regYout(registry_1_regyout),
    .regZout(registry_1_regzout), .corein0(coreout0), .clockout0(clockout0), .freqout0(freqout0),
    .output0(output0), .output1r(output1r), .output2r(output2r), .output3r(output3r), .output4r(output4r),
    .output5r(output5r), .output6r(output6r), .output7r(output7r), .output8r(output8r), .output9r(output9r),
    .output10r(output10r), .output11r(output11r), .output12r(output12r), .output13r(output13r),
    .output14r(output14r), .output15r(output15r), .output16r(output16r), .output1d(output1d),
    .output2d(output2d), .output3d(output3d), .output4d(output4d), .output5d(output5d), .output6d(output6d),
    .output7d(output7d), .output8d(output8d), .output9d(output9d), .output10d(output10d),
    .output11d(output11d), .output12d(output12d), .output13d(output13d), .output14d(output14d),
    .output15d(output15d), .output16d(output16d));
  BitSelector #(.group(8), .width(16)) bitselector_5 (.in(bitselector_4_out), .out(bitselector_5_out), .sel(1'b1));
  BitSelector #(.group(4), .width(16)) bitselector_6 (.in(bitselector_4_out), .out(bitselector_6_out), .sel(2'b01));
  BitSelector #(.group(4), .width(16)) bitselector_7 (.in(bitselector_4_out), .out(bitselector_7_out), .sel(2'b00));
  BitSelector #(.group(6)) bitselector_8 (.in(bitselector_5_out), .out(bitselector_8_out), .sel(1'b0));
  BitSelector #(.width(4)) bitselector_9 (.in(bitselector_6_out), .out(bitselector_9_out), .sel(2'b00));
  BitSelector #(.group(6)) bitselector_10 (.in(bitselector_5_out), .out(bitselector_10_out), .sel(1'b0));
  BitSelector #(.group(6)) bitselector_11 (.in(bitselector_5_out), .out(bitselector_11_out), .sel(1'b0));
  BitSelector #(.group(6), .width(64)) bitselector_12 (
    .in(registry_1_regzout), .out(bitselector_12_out), .sel(4'b0000));
  Comparator #(.mode("unsigned"), .width(4)) comparator_2 (
    .a(bitselector_7_out), .b(4'b0000), .eq(comparator_2_eq));  // open: gt, lt
  Counter #(.max('hffffffff), .trigger("falling"), .width(32)) counter_1 (
    .load(or_3_out), .D({32{1'b0}}), .count(comparator_2_eq), .Q(counter_1_q), .clk(clock_2_out));  // open: carry, up, clr
  Clock clock_2 (.out(clock_2_out));
  BitSelector #(.width(64)) bitselector_13 (.in(registry_1_regyout), .out(bitselector_13_out), .sel(bitselector_8_out));
  Comparator #(.mode("unsigned"), .width(4)) comparator_3 (
    .a(bitselector_7_out), .b(4'b0001), .eq(comparator_3_eq));  // open: gt, lt
  Comparator #(.mode("unsigned"), .width(4)) comparator_4 (
    .a(bitselector_7_out), .b(4'b0010), .eq(comparator_4_eq));  // open: gt, lt
  Comparator #(.mode("unsigned"), .width(4)) comparator_5 (
    .a(bitselector_7_out), .b(4'b0011), .eq(comparator_5_eq));  // open: gt, lt
  Counter #(.max('h1), .trigger("falling"), .width(1)) counter_2 (
    .load(comparator_12_eq), .D(1'b0), .count(comparator_5_eq), .Q(counter_2_q), .clk(clock_3_out));  // open: carry, up, clr
  Clock clock_3 (.out(clock_3_out));
  BitSelector #(.width(4)) bitselector_14 (.in(bitselector_6_out), .out(bitselector_14_out), .sel(2'b00));
  Comparator #(.mode("unsigned"), .width(4)) comparator_6 (
    .a(bitselector_7_out), .b(4'b0100), .eq(comparator_6_eq));  // open: gt, lt
  BitSelector #(.group(2), .width(4)) bitselector_15 (.in(bitselector_6_out), .out(bitselector_15_out), .sel(1'b0));
  Comparator #(.width(64)) comparator_7 (
    .a(registry_1_regyout), .b({64{1'b0}}), .eq(comparator_7_eq), .lt(comparator_7_lt));  // open: gt
  // FPComparator #(.fpwidth(64)) fpcomparator_1: pin names not known; wires that end beside it: registry_1_regyout, {64{1'b0}}, fpcomparator_1_p3, fpcomparator_1_p4
  Comparator #(.mode("unsigned"), .width(4)) comparator_8 (
    .a(bitselector_7_out), .b(4'b0101), .eq(comparator_8_eq));  // open: gt, lt
  assign and_1_out = registry_1_regxout & not_1_out;  // AND_Gate and_1, 64 bits wide
  Adder #(.width(64)) adder_1 (
    .a(registry_1_regzout), .b(registry_1_regyout), .out(adder_1_out), .cout(adder_1_cout));  // open: cin
  assign not_1_out = ~shifter_3_out;  // NOT_Gate not_1, 64 bits wide
  assign bit_extender_1_out = {{63{1'b0}}, adder_1_cout};  // Bit_Extender bit_extender_1
  Comparator #(.mode("unsigned"), .width(4)) comparator_9 (
    .a(bitselector_7_out), .b(4'b0110), .eq(comparator_9_eq));  // open: gt, lt
  Shifter #(.width(64)) shifter_1 (.in(registry_1_regyout), .\dist (bitselector_12_out), .out(shifter_1_out));
  Comparator #(.mode("unsigned"), .width(4)) comparator_10 (
    .a(bitselector_7_out), .b(4'b0111), .eq(comparator_10_eq));  // open: gt, lt
  FPAdder #(.fpwidth(64)) fpadder_1 (.a(registry_1_regyout), .b(registry_1_regzout), .out(fpadder_1_out));
  Comparator #(.mode("unsigned"), .width(32)) comparator_11 (
    .a(counter_1_q), .b({bitselector_2_out, bitselector_3_out}), .gt(comparator_11_gt),
    .eq(comparator_11_eq), .lt(comparator_11_lt));
  and and_2 (and_2_out, comparator_5_eq, comparator_12_lt);
  and and_3 (and_3_out, comparator_12_eq, not_2_out);
  not not_2 (not_2_out, bitselector_14_out);
  Comparator #(.mode("unsigned"), .width(1)) comparator_12 (
    .a(counter_2_q), .b(1'b1), .eq(comparator_12_eq), .lt(comparator_12_lt));  // open: gt
  and and_4 (and_4_out, comparator_12_eq, bitselector_14_out);
  assign not_3_out = ~shifter_2_out;  // NOT_Gate not_3, 64 bits wide
  Multiplexer #(.select(2)) multiplexer_1 (
    .in0(comparator_7_eq), .in1(comparator_7_lt), .in2(fpcomparator_1_p3), .in3(fpcomparator_1_p4),
    .out(multiplexer_1_out), .sel(bitselector_15_out));
  Shifter #(.width(64)) shifter_2 (.in(64'h1), .\dist (bitselector_10_out), .out(shifter_2_out));
  Multiplexer #(.select(4), .width(64)) multiplexer_2 (
    .in0(adder_1_out), .in1(or_2_out), .in2(subtractor_1_out), .in3(or_5_out), .in4(multiplier_1_out),
    .in5(multiplier_1_cout), .in6(divider_1_out), .in7(divider_1_rem), .in8(negator_1_out),
    .out(multiplexer_2_out), .sel(bitselector_6_out));  // open: in9, in10, in11, in12, in13, in14, in15
  assign or_2_out = and_1_out | shifter_3_out;  // OR_Gate or_2, 64 bits wide
  Shifter #(.width(64)) shifter_3 (.in(bit_extender_1_out), .\dist (bitselector_11_out), .out(shifter_3_out));
  Multiplexer #(.select(4), .width(64)) multiplexer_3 (
    .in0(shifter_1_out), .in1(shifter_4_out), .in2(shifter_5_out), .in3(shifter_7_out), .in4(shifter_8_out),
    .in5(buffer_1_out), .in6(not_5_out), .in7(or_6_out), .in8(and_9_out), .in9(nand_1_out), .in10(nor_1_out),
    .in11(xor_1_out), .in12(xnor_1_out), .out(multiplexer_3_out), .sel(bitselector_6_out));  // open: in13, in14, in15
  Shifter #(.shift("lr"), .width(64)) shifter_4 (
    .in(registry_1_regyout), .\dist (bitselector_12_out), .out(shifter_4_out));
  Multiplexer #(.select(4), .width(64)) multiplexer_4 (
    .in0(fpadder_1_out), .in1(fpsubtractor_1_out), .in2(fpmultiplier_1_out), .in3(fpdivider_1_out),
    .in4(fpnegator_1_p2), .in5(inttofp_1_p1), .in6(fptoint_1_p1), .in7(fptoint_2_p1), .in8(fptoint_3_p1),
    .in9(fptoint_4_p1), .out(multiplexer_4_out), .sel(bitselector_6_out));  // open: in10, in11, in12, in13, in14, in15
  FPSubtractor #(.fpwidth(64)) fpsubtractor_1 (
    .a(registry_1_regyout), .b(registry_1_regzout), .out(fpsubtractor_1_out));
  or or_3 (or_3_out, comparator_11_gt, comparator_11_eq);
  and and_5 (and_5_out, comparator_11_lt, comparator_2_eq);
  and and_6 (and_6_out, bitselector_13_out, comparator_3_eq);
  assign and_7_out = registry_1_regxout & not_3_out;  // AND_Gate and_7, 64 bits wide
  assign or_4_out = and_7_out | shifter_2_out;  // OR_Gate or_4, 64 bits wide
  Subtractor #(.width(64)) subtractor_1 (
    .a(registry_1_regyout), .b(registry_1_regzout), .out(subtractor_1_out), .bout(subtractor_1_bout));  // open: bin
  Shifter #(.shift("ar"), .width(64)) shifter_5 (
    .in(registry_1_regyout), .\dist (bitselector_12_out), .out(shifter_5_out));
  FPMultiplier #(.fpwidth(64)) fpmultiplier_1 (
    .a(registry_1_regyout), .b(registry_1_regzout), .out(fpmultiplier_1_out));
  Multiplexer multiplexer_5 (.in0(and_6_out), .in1(comparator_3_eq), .out(multiplexer_5_out), .sel(bitselector_9_out));
  Multiplexer #(.width(64)) multiplexer_6 (
    .in0(and_7_out), .in1(or_4_out), .out(multiplexer_6_out), .sel(multiplexer_1_out));
  assign and_8_out = registry_1_regxout & not_4_out;  // AND_Gate and_8, 64 bits wide
  assign not_4_out = ~shifter_6_out;  // NOT_Gate not_4, 64 bits wide
  assign bit_extender_2_out = {{63{1'b0}}, subtractor_1_bout};  // Bit_Extender bit_extender_2
  Shifter #(.width(64)) shifter_6 (.in(bit_extender_2_out), .\dist (bitselector_11_out), .out(shifter_6_out));
  Shifter #(.shift("rl"), .width(64)) shifter_7 (
    .in(registry_1_regyout), .\dist (bitselector_12_out), .out(shifter_7_out));
  FPDivider #(.fpwidth(64)) fpdivider_1 (.a(registry_1_regyout), .b(registry_1_regzout), .out(fpdivider_1_out));
  assign or_5_out = and_8_out | shifter_6_out;  // OR_Gate or_5, 64 bits wide
  assign not_5_out = ~registry_1_regyout;  // NOT_Gate not_5, 64 bits wide
  assign or_6_out = registry_1_regyout | registry_1_regzout;  // OR_Gate or_6, 64 bits wide
  assign buffer_1_out = registry_1_regyout;  // Buffer buffer_1, 64 bits wide
  Shifter #(.shift("rr"), .width(64)) shifter_8 (
    .in(registry_1_regyout), .\dist (bitselector_12_out), .out(shifter_8_out));
  // FPNegator #(.fpwidth(64)) fpnegator_1: pin names not known; wires that end beside it: registry_1_regyout, fpnegator_1_p2, registry_1_regyout
  // IntToFP #(.fpwidth(64), .width(64)) inttofp_1: pin names not known; wires that end beside it: inttofp_1_p1, registry_1_regyout
  Multiplier #(.mode("twosComplement"), .width(64)) multiplier_1 (
    .a(registry_1_regyout), .b(registry_1_regzout), .out(multiplier_1_out), .cout(multiplier_1_cout));  // open: cin
  assign nand_1_out = ~(registry_1_regyout & registry_1_regzout);  // NAND_Gate nand_1, 64 bits wide
  assign nor_1_out = ~(registry_1_regyout | registry_1_regzout);  // NOR_Gate nor_1, 64 bits wide
  assign and_9_out = registry_1_regyout & registry_1_regzout;  // AND_Gate and_9, 64 bits wide
  // FPToInt #(.fpwidth(64), .width(64)) fptoint_1: pin names not known; wires that end beside it: fptoint_1_p1, registry_1_regyout
  Divider #(.mode("twosComplement"), .width(64)) divider_1 (
    .a(registry_1_regyout), .b(registry_1_regzout), .out(divider_1_out), .rem(divider_1_rem));  // open: upper
  assign xnor_1_out = ~(registry_1_regyout ^ registry_1_regzout);  // XNOR_Gate xnor_1, 64 bits wide
  assign xor_1_out = registry_1_regyout ^ registry_1_regzout;  // XOR_Gate xor_1, 64 bits wide
  // FPToInt #(.fpwidth(64), .mode("floor"), .width(64)) fptoint_2: pin names not known; wires that end beside it: fptoint_2_p1, registry_1_regyout
  Negator #(.width(64)) negator_1 (.in(registry_1_regyout), .out(negator_1_out));
  // FPToInt #(.fpwidth(64), .mode("ceil"), .width(64)) fptoint_3: pin names not known; wires that end beside it: fptoint_3_p1, registry_1_regyout
  // FPToInt #(.fpwidth(64), .mode("truncate"), .width(64)) fptoint_4: pin names not known; wires that end beside it: fptoint_4_p1
  or or_7 (or_7_out, comparator_4_eq, and_3_out, comparator_6_eq, comparator_8_eq, comparator_9_eq, comparator_10_eq);
  or or_8 (or_8_out, comparator_2_eq, comparator_3_eq, comparator_4_eq, comparator_12_eq, comparator_6_eq, comparator_8_eq, comparator_9_eq, comparator_10_eq);
  Multiplexer #(.select(4), .width(64)) multiplexer_7 (
    .in0(multiplexer_12_out), .in1(multiplexer_12_out),
    .in2({{32{1'b0}}, bitselector_2_out, bitselector_3_out}), .in3(multiplexer_12_out),
    .in4(multiplexer_6_out), .in5(multiplexer_2_out), .in6(multiplexer_3_out), .in7(multiplexer_4_out),
    .out(multiplexer_7_out), .sel(bitselector_7_out));  // open: in8, in9, in10, in11, in12, in13, in14, in15
  BitSelector #(.group(26), .width(64)) bitselector_16 (.in(registry_1_regxout), .out(bitselector_16_out), .sel(2'b00));
  or or_9 (or_9_out, and_5_out, comparator_12_eq);
  Register #(.width(64)) register_2 (
    .D(registry_1_regyout), .en(and_2_out), .clk(clock_4_out), .Q(register_2_q));  // open: clr
  Clock clock_4 (.out(clock_4_out));
  Counter #(.max('h3ffffff), .width(26)) counter_3 (
    .load(multiplexer_5_out), .D(bitselector_16_out), .count(not_6_out), .Q(counter_3_q), .clk(clock_5_out));  // open: carry, up, clr
  not not_6 (not_6_out, or_9_out);
  Clock clock_5 (.out(clock_5_out));
  BitSelector #(.group(26), .width(64)) bitselector_17 (.in(register_2_q), .out(bitselector_17_out), .sel(2'b00));
  Register #(.width(1)) register_3 (.D(and_2_out), .en(1'b1), .clk(clock_4_out), .Q(register_3_q));  // open: clr
  Multiplexer #(.width(26)) multiplexer_8 (
    .in0(counter_3_q), .in1(bitselector_17_out), .out(multiplexer_8_out), .sel(register_3_q));
  Multiplexer #(.select(4), .width(26)) multiplexer_9 (
    .in0(counter_3_q), .in1(counter_3_q), .in2(counter_3_q), .in3(multiplexer_8_out), .in4(counter_3_q),
    .in5(counter_3_q), .in6(counter_3_q), .in7(counter_3_q), .out(multiplexer_9_out), .sel(bitselector_7_out));  // open: in8, in9, in10, in11, in12, in13, in14, in15
  Multiplexer #(.select(4)) multiplexer_10 (
    .in0(1'b0), .in1(1'b0), .in2(1'b0), .in3(and_4_out), .in4(1'b0), .in5(1'b0), .in6(1'b0), .in7(1'b0),
    .out(multiplexer_10_out), .sel(bitselector_7_out));  // open: in8, in9, in10, in11, in12, in13, in14, in15
  Multiplexer #(.select(4), .width(64)) multiplexer_11 (
    .in0({64{1'b0}}), .in1({64{1'b0}}), .in2({64{1'b0}}), .in3(registry_1_regxout), .in4({64{1'b0}}),
    .in5({64{1'b0}}), .in6({64{1'b0}}), .in7({64{1'b0}}), .out(multiplexer_11_out), .sel(bitselector_7_out));  // open: in8, in9, in10, in11, in12, in13, in14, in15
  BitSelector #(.group(2), .width(26)) bitselector_18 (.in(multiplexer_9_out), .out(bitselector_18_out), .sel(4'b1100));
  BitSelector #(.group(24), .width(26)) bitselector_19 (.in(multiplexer_9_out), .out(bitselector_19_out), .sel(1'b0));
  Clock clock_6 (.out(clock_6_out));
  Demultiplexer #(.select(2)) demultiplexer_1 (
    .out1(demultiplexer_1_out1), .out2(demultiplexer_1_out2), .out3(demultiplexer_1_out3),
    .in(multiplexer_10_out), .sel(bitselector_18_out));  // open: out0
  RAM #(.addrWidth(24), .dataWidth(64), .enables("line"), .\type ("nonvolatile")) ram_1 (
    .addr(bitselector_19_out), .clk(clock_6_out), .dout(ram_1_dout));  // open: we, din
  RAM #(.addrWidth(24), .dataWidth(64), .enables("line"), .\type ("nonvolatile")) ram_2 (
    .addr(bitselector_19_out), .we(demultiplexer_1_out1), .clk(clock_6_out), .din(multiplexer_11_out),
    .dout(ram_2_dout));
  RAM #(.addrWidth(24), .dataWidth(64), .enables("line"), .\type ("nonvolatile")) ram_3 (
    .addr(bitselector_19_out), .we(demultiplexer_1_out2), .clk(clock_6_out), .din(multiplexer_11_out),
    .dout(ram_3_dout));
  RAM #(.addrWidth(24), .dataWidth(64), .enables("line"), .\type ("nonvolatile")) ram_4 (
    .addr(bitselector_19_out), .we(demultiplexer_1_out3), .clk(clock_6_out), .din(multiplexer_11_out),
    .dout(ram_4_dout));
  Multiplexer #(.select(2), .width(64)) multiplexer_12 (
    .in0(ram_1_dout), .in1(ram_2_dout), .in2(ram_3_dout), .in3(ram_4_dout), .out(multiplexer_12_out),
    .sel(bitselector_18_out));
  BitSelector #(.group(8), .width(24)) bitselector_20 (.in(bitselector_19_out), .out(bitselector_20_out), .sel(2'b10));
  Comparator #(.mode("unsigned")) comparator_13 (
    .a(bitselector_20_out), .b({8{1'b0}}), .eq(comparator_13_eq));  // open: gt, lt
  and and_10 (and_10_out, demultiplexer_1_out2, comparator_13_eq);
  // RGB_Video #(.height(256), .scale(1), .width(256)) rgb_video_1: pin names not known; wires that end beside it: rgb_video_1_p1, and_10_out, rgb_video_1_p3, rgb_video_1_p4, rgb_video_1_p5
  Clock clock_7 (.out(rgb_video_1_p1));
  BitSelector #(.group(8), .width(24)) bitselector_21 (.in(bitselector_19_out), .out(rgb_video_1_p3), .sel(2'b00));
  BitSelector #(.group(8), .width(24)) bitselector_22 (.in(bitselector_19_out), .out(rgb_video_1_p4), .sel(2'b01));
  BitSelector #(.group(8), .width(64)) bitselector_23 (
    .in(multiplexer_11_out), .out(rgb_video_1_p5[7:0]), .sel(3'b000));
  BitSelector #(.group(8), .width(64)) bitselector_24 (
    .in(multiplexer_11_out), .out(rgb_video_1_p5[15:8]), .sel(3'b010));
  BitSelector #(.group(8), .width(64)) bitselector_25 (
    .in(multiplexer_11_out), .out(rgb_video_1_p5[23:16]), .sel(3'b100));
endmodule
module chip (
  input  [63:0] input1,
  input  [63:0] input2,
  input  [63:0] input3,
  input  [63:0] input4,
  input  [63:0] input5,
  input  [63:0] input6,
  input  [63:0] input7,
  input  [63:0] input8,
  input  [63:0] input9,
  input  [63:0] input10,
  input  [63:0] input11,
  input  [63:0] input12,
  input  [63:0] input13,
  input  [63:0] input14,
  input  [63:0] input15,
  input  [63:0] input16,
  output [63:0] output1,
  output [63:0] output2,
  output [63:0] output3,
  output [63:0] output4,
  output [63:0] output5,
  output [63:0] output6,
  output [63:0] output7,
  output [63:0] output8,
  output [63:0] output9,
  output [63:0] output10,
  output [63:0] output11,
  output [63:0] output12,
  output [63:0] output13,
  output [63:0] output14,
  output [63:0] output15,
  output [63:0] output16
);

  wire clock_1_out;
  wire [63:0] c0, d1A, d1B, d1C, d1D, d1E, d1F, d1G, d2A, d2B, d2C, d2D, d2E, d2F, d2G, d3A, d3B, d3C, d3D,
       d3E, d3F, d3G, d4A, d4B, d4C, d4D, d4E, d4F, d4G, d5A, d5B, d5C, d5D, d5E, d5F, d5G, d6A, d6B, d6C,
       d6D, d6E, d6F, d6G, d7A, d7B, d7C, d7D, d7E, d7F, d7G, d8A, d8B, d8C, d8D, d8E, d8F, d8G, d9A, d9B,
       d9C, d9D, d9E, d9F, d9G, d11, d12, d13, d14, d15, d16, d17, d18, d19, d21, d22, d23, d24, d25, d26,
       d27, d28, d29, d31, d32, d33, d34, d35, d36, d37, d38, d39, d41, d42, d43, d44, d45, d46, d47, d48,
       d49, d51, d52, d53, d54, d55, d56, d57, d58, d59, d61, d62, d63, d64, d65, d66, d67, d68, d69, d71,
       d72, d73, d74, d75, d76, d77, d78, d79, d81, d82, d83, d84, d85, d86, d87, d88, d89, d91, d92, d93,
       d94, d95, d96, d97, d98, d99, dA1, dA2, dA3, dA4, dA5, dA6, dA7, dA8, dA9, dAA, dAB, dAC, dAD, dAE,
       dAF, dAG, dB1, dB2, dB3, dB4, dB5, dB6, dB7, dB8, dB9, dBA, dBB, dBC, dBD, dBE, dBF, dBG, dC1, dC2,
       dC3, dC4, dC5, dC6, dC7, dC8, dC9, dCA, dCB, dCC, dCD, dCE, dCF, dCG, dD1, dD2, dD3, dD4, dD5, dD6,
       dD7, dD8, dD9, dDA, dDB, dDC, dDD, dDE, dDF, dDG, dE1, dE2, dE3, dE4, dE5, dE6, dE7, dE8, dE9, dEA,
       dEB, dEC, dED, dEE, dEF, dEG, dF1, dF2, dF3, dF4, dF5, dF6, dF7, dF8, dF9, dFA, dFB, dFC, dFD, dFE,
       dFF, dFG, dG1, dG2, dG3, dG4, dG5, dG6, dG7, dG8, dG9, dGA, dGB, dGC, dGD, dGE, dGF, dGG, r1, r2, r3,
       r4, r5, r6, r7, r8, r9, r10, r11, r12, r13, r14, r15, r16;

  core core1 (
    .corein0(64'hf000e0000f0000), .clockin0(c0), .freqin0(64'h5000000000), .input0(input1), .input1r(r1),
    .input2r(r2), .input3r(r3), .input4r(r4), .input5r(r5), .input6r(r6), .input7r(r7), .input8r(r8),
    .input9r(r9), .input10r(r10), .input11r(r11), .input12r(r12), .input13r(r13), .input14r(r14),
    .input1r5(r15), .input16r(r16), .input1d(d11), .input2d(d12), .input3d(d13), .input4d(d14),
    .input5d(d15), .input6d(d16), .input7d(d17), .input8d(d18), .input9d(d19), .input10d(d1A),
    .input11d(d1B), .input12d(d1C), .input13d(d1D), .input14d(d1E), .input15d(d1F), .input16d(d1G),
    .output0(output1), .output1r(r1), .output1d(d11), .output2d(d21), .output3d(d31), .output4d(d41),
    .output5d(d51), .output6d(d61), .output7d(d71), .output8d(d81), .output9d(d91), .output10d(dA1),
    .output11d(dB1), .output12d(dC1), .output13d(dD1), .output14d(dE1), .output15d(dF1), .output16d(dG1));  // open: coreout0, clockout0, freqout0, output2r, output3r, output4r, output5r, output6r, output7r, output8r, output9r, output10r, output11r, output12r, output13r, output14r, output15r, output16r
  core core5 (
    .corein0(64'hf400e4000f0004), .clockin0(c0), .freqin0(64'h5000000000), .input0(input5), .input1r(r1),
    .input2r(r2), .input3r(r3), .input4r(r4), .input5r(r5), .input6r(r6), .input7r(r7), .input8r(r8),
    .input9r(r9), .input10r(r10), .input11r(r11), .input12r(r12), .input13r(r13), .input14r(r14),
    .input1r5(r15), .input16r(r16), .input1d(d51), .input2d(d52), .input3d(d53), .input4d(d54),
    .input5d(d55), .input6d(d56), .input7d(d57), .input8d(d58), .input9d(d59), .input10d(d5A),
    .input11d(d5B), .input12d(d5C), .input13d(d5D), .input14d(d5E), .input15d(d5F), .input16d(d5G),
    .output0(output5), .output5r(r5), .output1d(d15), .output2d(d25), .output3d(d35), .output4d(d45),
    .output5d(d55), .output6d(d65), .output7d(d75), .output8d(d85), .output9d(d95), .output10d(dA5),
    .output11d(dB5), .output12d(dC5), .output13d(dD5), .output14d(dE5), .output15d(dF5), .output16d(dG5));  // open: coreout0, clockout0, freqout0, output1r, output2r, output3r, output4r, output6r, output7r, output8r, output9r, output10r, output11r, output12r, output13r, output14r, output15r, output16r
  core core9 (
    .corein0(64'hf800e8000f0008), .clockin0(c0), .freqin0(64'h5000000000), .input0(input9), .input1r(r1),
    .input2r(r2), .input3r(r3), .input4r(r4), .input5r(r5), .input6r(r6), .input7r(r7), .input8r(r8),
    .input9r(r9), .input10r(r10), .input11r(r11), .input12r(r12), .input13r(r13), .input14r(r14),
    .input1r5(r15), .input16r(r16), .input1d(d91), .input2d(d92), .input3d(d93), .input4d(d94),
    .input5d(d95), .input6d(d96), .input7d(d97), .input8d(d98), .input9d(d99), .input10d(d9A),
    .input11d(d9B), .input12d(d9C), .input13d(d9D), .input14d(d9E), .input15d(d9F), .input16d(d9G),
    .output0(output9), .output9r(r9), .output1d(d19), .output2d(d29), .output3d(d39), .output4d(d49),
    .output5d(d59), .output6d(d69), .output7d(d79), .output8d(d89), .output9d(d99), .output10d(dA9),
    .output11d(dB9), .output12d(dC9), .output13d(dD9), .output14d(dE9), .output15d(dF9), .output16d(dG9));  // open: coreout0, clockout0, freqout0, output1r, output2r, output3r, output4r, output5r, output6r, output7r, output8r, output10r, output11r, output12r, output13r, output14r, output15r, output16r
  core coreD (
    .corein0(64'hfc00ec000f000c), .clockin0(c0), .freqin0(64'h5000000000), .input0(input13), .input1r(r1),
    .input2r(r2), .input3r(r3), .input4r(r4), .input5r(r5), .input6r(r6), .input7r(r7), .input8r(r8),
    .input9r(r9), .input10r(r10), .input11r(r11), .input12r(r12), .input13r(r13), .input14r(r14),
    .input1r5(r15), .input16r(r16), .input1d(dD1), .input2d(dD2), .input3d(dD3), .input4d(dD4),
    .input5d(dD5), .input6d(dD6), .input7d(dD7), .input8d(dD8), .input9d(dD9), .input10d(dDA),
    .input11d(dDB), .input12d(dDC), .input13d(dDD), .input14d(dDE), .input15d(dDF), .input16d(dDG),
    .output0(output13), .output13r(r13), .output1d(d1D), .output2d(d2D), .output3d(d3D), .output4d(d4D),
    .output5d(d5D), .output6d(d6D), .output7d(d7D), .output8d(d8D), .output9d(d9D), .output10d(dAD),
    .output11d(dBD), .output12d(dCD), .output13d(dDD), .output14d(dED), .output15d(dFD), .output16d(dGD));  // open: coreout0, clockout0, freqout0, output1r, output2r, output3r, output4r, output5r, output6r, output7r, output8r, output9r, output10r, output11r, output12r, output14r, output15r, output16r
  core core2 (
    .corein0(64'hf100e1000f0001), .clockin0(c0), .freqin0(64'h5000000000), .input0(input2), .input1r(r1),
    .input2r(r2), .input3r(r3), .input4r(r4), .input5r(r5), .input6r(r6), .input7r(r7), .input8r(r8),
    .input9r(r9), .input10r(r10), .input11r(r11), .input12r(r12), .input13r(r13), .input14r(r14),
    .input1r5(r15), .input16r(r16), .input1d(d21), .input2d(d22), .input3d(d23), .input4d(d24),
    .input5d(d25), .input6d(d26), .input7d(d27), .input8d(d28), .input9d(d29), .input10d(d2A),
    .input11d(d2B), .input12d(d2C), .input13d(d2D), .input14d(d2E), .input15d(d2F), .input16d(d2G),
    .output0(output2), .output2r(r2), .output1d(d12), .output2d(d22), .output3d(d32), .output4d(d42),
    .output5d(d52), .output6d(d62), .output7d(d72), .output8d(d82), .output9d(d92), .output10d(dA2),
    .output11d(dB2), .output12d(dC2), .output13d(dD2), .output14d(dE2), .output15d(dF2), .output16d(dG2));  // open: coreout0, clockout0, freqout0, output1r, output3r, output4r, output5r, output6r, output7r, output8r, output9r, output10r, output11r, output12r, output13r, output14r, output15r, output16r
  core core6 (
    .corein0(64'hf500e5000f0005), .clockin0(c0), .freqin0(64'h5000000000), .input0(input6), .input1r(r1),
    .input2r(r2), .input3r(r3), .input4r(r4), .input5r(r5), .input6r(r6), .input7r(r7), .input8r(r8),
    .input9r(r9), .input10r(r10), .input11r(r11), .input12r(r12), .input13r(r13), .input14r(r14),
    .input1r5(r15), .input16r(r16), .input1d(d61), .input2d(d62), .input3d(d63), .input4d(d64),
    .input5d(d65), .input6d(d66), .input7d(d67), .input8d(d68), .input9d(d69), .input10d(d6A),
    .input11d(d6B), .input12d(d6C), .input13d(d6D), .input14d(d6E), .input15d(d6F), .input16d(d6G),
    .output0(output6), .output6r(r6), .output1d(d16), .output2d(d26), .output3d(d36), .output4d(d46),
    .output5d(d56), .output6d(d66), .output7d(d76), .output8d(d86), .output9d(d96), .output10d(dA6),
    .output11d(dB6), .output12d(dC6), .output13d(dD6), .output14d(dE6), .output15d(dF6), .output16d(dG6));  // open: coreout0, clockout0, freqout0, output1r, output2r, output3r, output4r, output5r, output7r, output8r, output9r, output10r, output11r, output12r, output13r, output14r, output15r, output16r
  core coreA (
    .corein0(64'hf900e9000f0009), .clockin0(c0), .freqin0(64'h5000000000), .input0(input10), .input1r(r1),
    .input2r(r2), .input3r(r3), .input4r(r4), .input5r(r5), .input6r(r6), .input7r(r7), .input8r(r8),
    .input9r(r9), .input10r(r10), .input11r(r11), .input12r(r12), .input13r(r13), .input14r(r14),
    .input1r5(r15), .input16r(r16), .input1d(dA1), .input2d(dA2), .input3d(dA3), .input4d(dA4),
    .input5d(dA5), .input6d(dA6), .input7d(dA7), .input8d(dA8), .input9d(dA9), .input10d(dAA),
    .input11d(dAB), .input12d(dAC), .input13d(dAD), .input14d(dAE), .input15d(dAF), .input16d(dAG),
    .output0(output10), .output10r(r10), .output1d(d1A), .output2d(d2A), .output3d(d3A), .output4d(d4A),
    .output5d(d5A), .output6d(d6A), .output7d(d7A), .output8d(d8A), .output9d(d9A), .output10d(dAA),
    .output11d(dBA), .output12d(dCA), .output13d(dDA), .output14d(dEA), .output15d(dFA), .output16d(dGA));  // open: coreout0, clockout0, freqout0, output1r, output2r, output3r, output4r, output5r, output6r, output7r, output8r, output9r, output11r, output12r, output13r, output14r, output15r, output16r
  core coreE (
    .corein0(64'hfd00ed000f000d), .clockin0(c0), .freqin0(64'h5000000000), .input0(input14), .input1r(r1),
    .input2r(r2), .input3r(r3), .input4r(r4), .input5r(r5), .input6r(r6), .input7r(r7), .input8r(r8),
    .input9r(r9), .input10r(r10), .input11r(r11), .input12r(r12), .input13r(r13), .input14r(r14),
    .input1r5(r15), .input16r(r16), .input1d(dE1), .input2d(dE2), .input3d(dE3), .input4d(dE4),
    .input5d(dE5), .input6d(dE6), .input7d(dE7), .input8d(dE8), .input9d(dE9), .input10d(dEA),
    .input11d(dEB), .input12d(dEC), .input13d(dED), .input14d(dEE), .input15d(dEF), .input16d(dEG),
    .output0(output14), .output14r(r14), .output1d(d1E), .output2d(d2E), .output3d(d3E), .output4d(d4E),
    .output5d(d5E), .output6d(d6E), .output7d(d7E), .output8d(d8E), .output9d(d9E), .output10d(dAE),
    .output11d(dBE), .output12d(dCE), .output13d(dDE), .output14d(dEE), .output15d(dFE), .output16d(dGE));  // open: coreout0, clockout0, freqout0, output1r, output2r, output3r, output4r, output5r, output6r, output7r, output8r, output9r, output10r, output11r, output12r, output13r, output15r, output16r
  core core3 (
    .corein0(64'hf200e2000f0002), .clockin0(c0), .freqin0(64'h5000000000), .input0(input3), .input1r(r1),
    .input2r(r2), .input3r(r3), .input4r(r4), .input5r(r5), .input6r(r6), .input7r(r7), .input8r(r8),
    .input9r(r9), .input10r(r10), .input11r(r11), .input12r(r12), .input13r(r13), .input14r(r14),
    .input1r5(r15), .input16r(r16), .input1d(d31), .input2d(d32), .input3d(d33), .input4d(d34),
    .input5d(d35), .input6d(d36), .input7d(d37), .input8d(d38), .input9d(d39), .input10d(d3A),
    .input11d(d3B), .input12d(d3C), .input13d(d3D), .input14d(d3E), .input15d(d3F), .input16d(d3G),
    .output0(output3), .output3r(r3), .output1d(d13), .output2d(d23), .output3d(d33), .output4d(d43),
    .output5d(d53), .output6d(d63), .output7d(d73), .output8d(d83), .output9d(d93), .output10d(dA3),
    .output11d(dB3), .output12d(dC3), .output13d(dD3), .output14d(dE3), .output15d(dF3), .output16d(dG3));  // open: coreout0, clockout0, freqout0, output1r, output2r, output4r, output5r, output6r, output7r, output8r, output9r, output10r, output11r, output12r, output13r, output14r, output15r, output16r
  core core7 (
    .corein0(64'hf600e6000f0006), .clockin0(c0), .freqin0(64'h5000000000), .input0(input7), .input1r(r1),
    .input2r(r2), .input3r(r3), .input4r(r4), .input5r(r5), .input6r(r6), .input7r(r7), .input8r(r8),
    .input9r(r9), .input10r(r10), .input11r(r11), .input12r(r12), .input13r(r13), .input14r(r14),
    .input1r5(r15), .input16r(r16), .input1d(d71), .input2d(d72), .input3d(d73), .input4d(d74),
    .input5d(d75), .input6d(d76), .input7d(d77), .input8d(d78), .input9d(d79), .input10d(d7A),
    .input11d(d7B), .input12d(d7C), .input13d(d7D), .input14d(d7E), .input15d(d7F), .input16d(d7G),
    .output0(output7), .output7r(r7), .output1d(d17), .output2d(d27), .output3d(d37), .output4d(d47),
    .output5d(d57), .output6d(d67), .output7d(d77), .output8d(d87), .output9d(d97), .output10d(dA7),
    .output11d(dB7), .output12d(dC7), .output13d(dD7), .output14d(dE7), .output15d(dF7), .output16d(dG7));  // open: coreout0, clockout0, freqout0, output1r, output2r, output3r, output4r, output5r, output6r, output8r, output9r, output10r, output11r, output12r, output13r, output14r, output15r, output16r
  core coreB (
    .corein0(64'hfa00ea000f000a), .clockin0(c0), .freqin0(64'h5000000000), .input0(input11), .input1r(r1),
    .input2r(r2), .input3r(r3), .input4r(r4), .input5r(r5), .input6r(r6), .input7r(r7), .input8r(r8),
    .input9r(r9), .input10r(r10), .input11r(r11), .input12r(r12), .input13r(r13), .input14r(r14),
    .input1r5(r15), .input16r(r16), .input1d(dB1), .input2d(dB2), .input3d(dB3), .input4d(dB4),
    .input5d(dB5), .input6d(dB6), .input7d(dB7), .input8d(dB8), .input9d(dB9), .input10d(dBA),
    .input11d(dBB), .input12d(dBC), .input13d(dBD), .input14d(dBE), .input15d(dBF), .input16d(dBG),
    .output0(output11), .output11r(r11), .output1d(d1B), .output2d(d2B), .output3d(d3B), .output4d(d4B),
    .output5d(d5B), .output6d(d6B), .output7d(d7B), .output8d(d8B), .output9d(d9B), .output10d(dAB),
    .output11d(dBB), .output12d(dCB), .output13d(dDB), .output14d(dEB), .output15d(dFB), .output16d(dGB));  // open: coreout0, clockout0, freqout0, output1r, output2r, output3r, output4r, output5r, output6r, output7r, output8r, output9r, output10r, output12r, output13r, output14r, output15r, output16r
  core coreF (
    .corein0(64'hfe00ee000f000e), .clockin0(c0), .freqin0(64'h5000000000), .input0(input15), .input1r(r1),
    .input2r(r2), .input3r(r3), .input4r(r4), .input5r(r5), .input6r(r6), .input7r(r7), .input8r(r8),
    .input9r(r9), .input10r(r10), .input11r(r11), .input12r(r12), .input13r(r13), .input14r(r14),
    .input1r5(r15), .input16r(r16), .input1d(dF1), .input2d(dF2), .input3d(dF3), .input4d(dF4),
    .input5d(dF5), .input6d(dF6), .input7d(dF7), .input8d(dF8), .input9d(dF9), .input10d(dFA),
    .input11d(dFB), .input12d(dFC), .input13d(dFD), .input14d(dFE), .input15d(dFF), .input16d(dFG),
    .output0(output15), .output15r(r15), .output1d(d1F), .output2d(d2F), .output3d(d3F), .output4d(d4F),
    .output5d(d5F), .output6d(d6F), .output7d(d7F), .output8d(d8F), .output9d(d9F), .output10d(dAF),
    .output11d(dBF), .output12d(dCF), .output13d(dDF), .output14d(dEF), .output15d(dFF), .output16d(dGF));  // open: coreout0, clockout0, freqout0, output1r, output2r, output3r, output4r, output5r, output6r, output7r, output8r, output9r, output10r, output11r, output12r, output13r, output14r, output16r
  core core4 (
    .corein0(64'hf300e3000f0003), .clockin0(c0), .freqin0(64'h5000000000), .input0(input4), .input1r(r1),
    .input2r(r2), .input3r(r3), .input4r(r4), .input5r(r5), .input6r(r6), .input7r(r7), .input8r(r8),
    .input9r(r9), .input10r(r10), .input11r(r11), .input12r(r12), .input13r(r13), .input14r(r14),
    .input1r5(r15), .input16r(r16), .input1d(d41), .input2d(d42), .input3d(d43), .input4d(d44),
    .input5d(d45), .input6d(d46), .input7d(d47), .input8d(d48), .input9d(d49), .input10d(d4A),
    .input11d(d4B), .input12d(d4C), .input13d(d4D), .input14d(d4E), .input15d(d4F), .input16d(d4G),
    .output0(output4), .output4r(r4), .output1d(d14), .output2d(d24), .output3d(d34), .output4d(d44),
    .output5d(d54), .output6d(d64), .output7d(d74), .output8d(d84), .output9d(d94), .output10d(dA4),
    .output11d(dB4), .output12d(dC4), .output13d(dD4), .output14d(dE4), .output15d(dF4), .output16d(dG4));  // open: coreout0, clockout0, freqout0, output1r, output2r, output3r, output5r, output6r, output7r, output8r, output9r, output10r, output11r, output12r, output13r, output14r, output15r, output16r
  core core8 (
    .corein0(64'hf700e7000f0007), .clockin0(c0), .freqin0(64'h5000000000), .input0(input8), .input1r(r1),
    .input2r(r2), .input3r(r3), .input4r(r4), .input5r(r5), .input6r(r6), .input7r(r7), .input8r(r8),
    .input9r(r9), .input10r(r10), .input11r(r11), .input12r(r12), .input13r(r13), .input14r(r14),
    .input1r5(r15), .input16r(r16), .input1d(d81), .input2d(d82), .input3d(d83), .input4d(d84),
    .input5d(d85), .input6d(d86), .input7d(d87), .input8d(d88), .input9d(d89), .input10d(d8A),
    .input11d(d8B), .input12d(d8C), .input13d(d8D), .input14d(d8E), .input15d(d8F), .input16d(d8G),
    .output0(output8), .output8r(r8), .output1d(d18), .output2d(d28), .output3d(d38), .output4d(d48),
    .output5d(d58), .output6d(d68), .output7d(d78), .output8d(d88), .output9d(d98), .output10d(dA8),
    .output11d(dB8), .output12d(dC8), .output13d(dD8), .output14d(dE8), .output15d(dF8), .output16d(dG8));  // open: coreout0, clockout0, freqout0, output1r, output2r, output3r, output4r, output5r, output6r, output7r, output9r, output10r, output11r, output12r, output13r, output14r, output15r, output16r
  core coreC (
    .corein0(64'hfb00eb000f000b), .clockin0(c0), .freqin0(64'h5000000000), .input0(input12), .input1r(r1),
    .input2r(r2), .input3r(r3), .input4r(r4), .input5r(r5), .input6r(r6), .input7r(r7), .input8r(r8),
    .input9r(r9), .input10r(r10), .input11r(r11), .input12r(r12), .input13r(r13), .input14r(r14),
    .input1r5(r15), .input16r(r16), .input1d(dC1), .input2d(dC2), .input3d(dC3), .input4d(dC4),
    .input5d(dC5), .input6d(dC6), .input7d(dC7), .input8d(dC8), .input9d(dC9), .input10d(dCA),
    .input11d(dCB), .input12d(dCC), .input13d(dCD), .input14d(dCE), .input15d(dCF), .input16d(dCG),
    .output0(output12), .output12r(r12), .output1d(d1C), .output2d(d2C), .output3d(d3C), .output4d(d4C),
    .output5d(d5C), .output6d(d6C), .output7d(d7C), .output8d(d8C), .output9d(d9C), .output10d(dAC),
    .output11d(dBC), .output12d(dCC), .output13d(dDC), .output14d(dEC), .output15d(dFC), .output16d(dGC));  // open: coreout0, clockout0, freqout0, output1r, output2r, output3r, output4r, output5r, output6r, output7r, output8r, output9r, output10r, output11r, output13r, output14r, output15r, output16r
  core coreG (
    .corein0(64'hff00ef000f000f), .clockin0(c0), .freqin0(64'h5000000000), .input0(input16), .input1r(r1),
    .input2r(r2), .input3r(r3), .input4r(r4), .input5r(r5), .input6r(r6), .input7r(r7), .input8r(r8),
    .input9r(r9), .input10r(r10), .input11r(r11), .input12r(r12), .input13r(r13), .input14r(r14),
    .input1r5(r15), .input16r(r16), .input1d(dG1), .input2d(dG2), .input3d(dG3), .input4d(dG4),
    .input5d(dG5), .input6d(dG6), .input7d(dG7), .input8d(dG8), .input9d(dG9), .input10d(dGA),
    .input11d(dGB), .input12d(dGC), .input13d(dGD), .input14d(dGE), .input15d(dGF), .input16d(dGG),
    .output0(output16), .output16r(r16), .output1d(d1G), .output2d(d2G), .output3d(d3G), .output4d(d4G),
    .output5d(d5G), .output6d(d6G), .output7d(d7G), .output8d(d8G), .output9d(d9G), .output10d(dAG),
    .output11d(dBG), .output12d(dCG), .output13d(dDG), .output14d(dEG), .output15d(dFG), .output16d(dGG));  // open: coreout0, clockout0, freqout0, output1r, output2r, output3r, output4r, output5r, output6r, output7r, output8r, output9r, output10r, output11r, output12r, output13r, output14r, output15r
  Counter #(.max('hffffffffffffffff), .width(64)) counter_1 (
    .Q(c0), .clk(clock_1_out));  // open: load, D, count, carry, up, clr
  Clock clock_1 (.out(clock_1_out));
endmodule
